// Logisim project lab1.3.circ as structural Verilog: 1 circuit, main circuit main
module main (
  input  D0,
  input  D1,
  input  S,
  output Y
);

  wire AND1_out, AND2_out, not_1_out;

  // Probe on S
  // Probe on not_1_out
  and AND1 (AND1_out, D0, not_1_out);
  and AND2 (AND2_out, D1, S);
  not not_1 (not_1_out, S);
  or OR (Y, AND1_out, AND2_out);

  // Notes on the sheet:
  //   输入引脚
  //   请勿修改引脚名称及电路封装外观
  //   提示：使用独立逻辑门实现二选一多路选择器，禁止直接使用选择器组件。
  //   输出引脚
endmodule
