// Logisim project lab1.4.circ as structural Verilog: 1 circuit, main circuit main
module main (
  input  D0,
  input  D1,
  input  S,
  output Y
);

  wire transistor_1_out, transmission_1_p1, transmission_1_p3;

  Transistor transistor_1 (.in(1'b1), .out(transistor_1_out), .gate(S));
  Transistor #(.\type ("n")) transistor_2 (.in(1'b0), .out(transistor_1_out), .gate(S));
  // Transmission_Gate transmission_1: pin names not known; wires that end beside it: transmission_1_p1, transmission_1_p1, transmission_1_p3, D0, transmission_1_p3, S, transistor_1_out, Y
  // Transmission_Gate transmission_2: pin names not known; wires that end beside it: 1'b0, D1, transistor_1_out, S, Y

  // Notes on the sheet:
  //   输入引脚
  //   请勿修改引脚名称及电路封装外观
  //   提示：使用传输门和晶体管来实现二选一多路选择器，禁止直接使用选择器组件。
  //   输出引脚
endmodule
