// Logisim project lab1.6.circ as structural Verilog: 1 circuit, main circuit main
module main (
  input  [3:0] INPUT,
  input  [1:0] SELECT,
  input  OUTPUT
);

  wire main_1_y, main_2_y;

  lab1_3_main main_1 (.D0(INPUT[0]), .D1(INPUT[1]), .S(SELECT[0]), .Y(main_1_y));
  lab1_3_main main_2 (.D0(INPUT[2]), .D1(INPUT[3]), .S(SELECT[0]), .Y(main_2_y));
  lab1_3_main main_3 (.D0(main_1_y), .D1(main_2_y), .S(SELECT[1]), .Y(OUTPUT));

  // Other names for the same wires on the sheet: DATA[3:0] = INPUT; S[1:0] = SELECT; Y = OUTPUT
endmodule
