// Logisim project lab1.思考题2.circ as structural Verilog: 1 circuit, main circuit main
module main (
  input  [3:0] X,
  output [3:0] out_2
);

  xor xor_1 (out_2[0], X[0], X[1]);
  xor xor_2 (out_2[1], X[1], X[2]);
  xor xor_3 (out_2[2], X[2], X[3]);

  assign out_2[3] = X[3];
endmodule
