// Logisim project lab1.思考题3.circ as structural Verilog: 1 circuit, main circuit main
module main (
  input  [3:0] X,
  output Y
);

  wire xor_1_out, xor_3_out;

  xor xor_1 (xor_1_out, X[0], X[1]);
  xor xor_2 (Y, xor_1_out, xor_3_out);
  xor xor_3 (xor_3_out, X[2], X[3]);
endmodule
