// Logisim project lab2思考题1.circ as structural Verilog: 1 circuit, main circuit main
module main (
  input  [3:0] X,
  input  [3:0] Y,
  input  Cin,
  output [3:0] F,
  output Cout,
  output out_6,
  output out_7,
  output out_8,
  output out_9
);

  wire FA0_cout, FA1_cout, FA2_cout;

  Hex_Digit_Display hex_digit_display_1 (.value(X));  // open: dp
  Hex_Digit_Display hex_digit_display_2 (.value(Y));  // open: dp
  FA FA0 (.A(X[0]), .B(Y[0]), .Cin(Cin), .Cout(FA0_cout), .F(F[0]));
  Hex_Digit_Display hex_digit_display_3 (.value(F));  // open: dp
  FA FA1 (.A(X[1]), .B(Y[1]), .Cin(FA0_cout), .Cout(FA1_cout), .F(F[1]));
  FA FA2 (.A(X[2]), .B(Y[2]), .Cin(FA1_cout), .Cout(FA2_cout), .F(F[2]));
  FA FA3 (.A(X[3]), .B(Y[3]), .Cin(FA2_cout), .Cout(Cout), .F(F[3]));
  xor xor_1 (out_7, Cout, FA2_cout);
  xor xor_2 (out_8, Cout, Cin);
  and and_1 (out_6, ~F[1], ~F[0], ~F[2], ~F[3]);  // AND_Gate

  assign out_9 = F[3];

  // Other names for the same wires on the sheet: CF = out_8; OF = out_7; SUM[3:0] = F; SF = F[3]; ZF = out_6;
  //   操作数x[3:0] = X; 操作数y[3:0] = Y

  // Notes on the sheet:
  //   输入引脚
  //   +
  //   =
  //   请勿修改引脚名称、电路名称及电路封装外观
  //   提示：使用独立逻辑门及全加器FA子电路实现4位二进制数加减法器，禁止直接使用加减法器组件。
  //   输出引脚
endmodule
