// Logisim project lab2思考题3.circ as structural Verilog: 1 circuit, main circuit main
module main (
  input  [3:0] in_1,
  input  [3:0] in_2,
  output out_3,
  output out_4,
  output out_5
);

  wire and_1_out, and_2_out, and_3_out, and_4_out, and_5_out, and_6_out, and_8_out, multiplexer_1_out,
       not_1_out, not_2_out, not_3_out, not_4_out, not_5_out, not_6_out, or_1_out, or_2_out, xor_1_out,
       xor_2_out, xor_3_out, xor_4_out;

  not not_1 (not_1_out, xor_1_out);
  xor xor_1 (xor_1_out, in_1[3], in_2[3]);
  not not_2 (not_2_out, xor_2_out);
  xor xor_2 (xor_2_out, in_1[2], in_2[2]);
  xor xor_3 (xor_3_out, in_1[1], in_2[1]);
  not not_3 (not_3_out, xor_3_out);
  xor xor_4 (xor_4_out, in_1[0], in_2[0]);
  not not_4 (not_4_out, xor_4_out);
  and and_1 (and_1_out, ~in_2[3], in_1[3]);  // AND_Gate
  and and_2 (and_2_out, not_1_out, ~in_2[2], in_1[2]);  // AND_Gate
  and and_3 (and_3_out, not_1_out, not_2_out, ~in_2[1], in_1[1]);  // AND_Gate
  and and_4 (and_4_out, not_1_out, not_2_out, not_3_out, ~in_2[0], in_2[3]);  // AND_Gate
  and and_5 (and_5_out, ~in_1[3], in_2[3]);  // AND_Gate
  and and_6 (and_6_out, in_1[3], ~in_2[3]);  // AND_Gate
  and and_7 (out_4, not_1_out, not_2_out, not_3_out, not_4_out);
  or or_1 (or_1_out, and_1_out, and_2_out, and_3_out, and_4_out);
  not not_5 (not_5_out, or_1_out);
  and and_8 (and_8_out, in_2[3], in_1[3]);
  or or_2 (or_2_out, and_5_out, multiplexer_1_out);
  Multiplexer #(.enable("false")) multiplexer_1 (
    .in0(or_1_out), .in1(not_5_out), .out(multiplexer_1_out), .sel(and_8_out));
  and and_9 (out_5, or_2_out, not_6_out);
  not not_6 (not_6_out, and_6_out);
  xnor xnor_1 (out_3, out_4, out_5);

  // Other names for the same wires on the sheet: Equal = out_4; Great = out_5; Less = out_3; X[3:0] = in_1;
  //   Y[3:0] = in_2
endmodule
