// Logisim project lab3思考题1.circ as structural Verilog: 1 circuit, main circuit main
module main (
  input  CLR,
  input  in_2,
  input  in_3
);

  wire clock_1_out, not_1_out, undriven, xor_1_out;
  wire [3:0] shrg4u_1_q0, shrg4u_2_q0;

  Clock clock_1 (.out(clock_1_out));
  not not_1 (not_1_out, 1'b1);
  SHRG4U shrg4u_1 (
    .CLK(clock_1_out), .CLR_L(CLR), .RIN(undriven), .Q3(shrg4u_1_q0[3]), .Q2(shrg4u_1_q0[2]), .D3(not_1_out),
    .D2(not_1_out), .D1(not_1_out), .Q1(shrg4u_1_q0[1]), .Q0(shrg4u_1_q0[0]), .D0(1'b1), .LIN(xor_1_out),
    .S1(in_2), .S0(in_3));
  SHRG4U shrg4u_2 (
    .CLK(clock_1_out), .CLR_L(CLR), .Q3(shrg4u_2_q0[3]), .Q2(shrg4u_2_q0[2]), .D3(shrg4u_2_q0[2]),
    .D2(shrg4u_2_q0[1]), .D1(shrg4u_2_q0[0]), .Q1(shrg4u_2_q0[1]), .Q0(shrg4u_2_q0[0]), .D0(shrg4u_1_q0[3]),
    .S1(1'b1), .S0(1'b1));  // open: RIN, LIN
  xor xor_1 (xor_1_out, shrg4u_2_q0[3], shrg4u_2_q0[2]);
  Hex_Digit_Display hex_digit_display_1 (.value(shrg4u_2_q0));  // open: dp
  Hex_Digit_Display hex_digit_display_2 (.value(shrg4u_1_q0));  // open: dp
endmodule
