// Logisim project lab3思考题3.circ as structural Verilog: 1 circuit, main circuit main
module main (
  input  [4:0] R1_num,
  input  [4:0] R2_num,
  input  [4:0] Write_Reg_num,
  input  [31:0] Din,
  input  Write_Enable,
  output [31:0] Reg1Out,
  output [31:0] Reg2Out
);

  wire clock_1_out;

  Clock clock_1 (.out(clock_1_out));
  lab3_4_main main_1 (
    .R1_num(R1_num), .R2_num(R2_num), .Din(Din), .Reg1Out(Reg1Out), .Write_Reg_num(Write_Reg_num),
    .Write_Enable(Write_Enable), .Clock(clock_1_out), .Reg2Out(Reg2Out));
endmodule
