// Logisim project lab4.3.circ as structural Verilog: 1 circuit, main circuit main
// 加法器
module main (
  input  Cin,
  input  [31:0] X,
  input  [31:0] Y,
  output OF,
  output Cout,
  output CF,
  output ZF,
  output [31:0] S,
  output SF
);

  wire and_1_out, and_2_out, main_2_c16, or_2_out, or_3_out, or_4_out, or_5_out, or_6_out;

  lab4_2_main main_1 (.X(X[31:16]), .Y(Y[31:16]), .C0(main_2_c16), .S(S[31:16]), .C16(Cout));  // open: Pg, Gg
  xor xor_1 (CF, Cin, Cout);
  lab4_2_main main_2 (.X(X[15:0]), .Y(Y[15:0]), .C0(Cin), .S(S[15:0]), .C16(main_2_c16));  // open: Pg, Gg
  and and_1 (and_1_out, ~X[31], ~Y[31], S[31]);  // AND_Gate
  and and_2 (and_2_out, X[31], Y[31], ~S[31]);  // AND_Gate
  or or_1 (OF, and_1_out, and_2_out);
  // Probe on X
  // Probe on Y
  // Probe on S
  or or_2 (or_2_out, S[31], S[30], S[29], S[28], S[27], S[26], S[25], S[24]);
  or or_3 (or_3_out, S[23], S[22], S[21], S[20], S[19], S[18], S[17], S[16]);
  not not_1 (ZF, or_4_out);
  or or_4 (or_4_out, or_2_out, or_3_out, or_5_out, or_6_out);
  or or_5 (or_5_out, S[15], S[14], S[13], S[12], S[11], S[10], S[9], S[8]);
  or or_6 (or_6_out, S[7], S[6], S[5], S[4], S[3], S[2], S[1], S[0]);

  assign SF = S[31];

  // Notes on the sheet:
  //   Cin: pull=down
  //   X: pull=down
  //   Y: pull=down
  //   输入引脚区
  //   输出引脚区
  //   请勿修改引脚名称、电路名称及电路封装外观
  //   提示：使用两个16位并行加法器子电路串行实现32位快速加法器
  //   功能说明:32位Adder  S=X+Y，Cout为最高位进位位，Cin为进位输入， S为和，溢出OF、进位CF、零ZF、符号SF。
  //   +
  //   =
  //   无符号加法
endmodule
