// Logisim project lab4思考题1.circ as structural Verilog: 3 circuits, main circuit main
module main (
  input  [4:0] X,
  input  [4:0] Y,
  output [9:0] \乘积 
);

  wire fa_2_cout, fa_2_f, fa_3_cout, fa_4_cout, fa_4_f, fa_5_cout, fa_5_f, fa_6_cout, fa_7_cout, fa_7_f,
       fa_8_cout, fa_8_f, fa_9_cout, fa_9_f, fa_10_cout, fa_11_cout, fa_11_f, fa_12_cout, fa_12_f,
       fa_13_cout, fa_13_f, fa_14_cout, fa_15_cout, fa_15_f, fa_16_cout, fa_16_f, fa_17_cout, fa_18_cout,
       fa_18_f, fa_19_cout, fa_20_cout, X0Y1, X0Y2, X0Y3, X0Y4, X1Y0, X1Y1, X1Y2, X1Y3, X1Y4, X2Y0, X2Y1,
       X2Y2, X2Y3, X2Y4, X3Y0, X3Y1, X3Y2, X3Y3, X3Y4, X4Y0, X4Y1, X4Y2, X4Y3, X4Y4;

  FA fa (.Cout(\乘积 [9]), .F(\乘积 [8]), .Cin(fa_2_cout), .X(fa_3_cout), .Y(X4Y4));
  // Probe on X
  FA fa_2 (.Cout(fa_2_cout), .F(fa_2_f), .Cin(fa_4_cout), .X(X3Y4), .Y(X4Y3));
  FA fa_3 (.Cout(fa_3_cout), .F(\乘积 [7]), .Cin(fa_5_cout), .X(fa_6_cout), .Y(fa_2_f));
  FA fa_4 (.Cout(fa_4_cout), .F(fa_4_f), .Cin(fa_7_cout), .X(X3Y3), .Y(X4Y2));
  FA fa_5 (.Cout(fa_5_cout), .F(fa_5_f), .Cin(fa_8_cout), .X(X2Y4), .Y(fa_4_f));
  FA fa_6 (.Cout(fa_6_cout), .F(\乘积 [6]), .Cin(fa_9_cout), .X(fa_10_cout), .Y(fa_5_f));
  // Probe on Y
  FA fa_7 (.Cout(fa_7_cout), .F(fa_7_f), .Cin(fa_11_cout), .X(X3Y2), .Y(X4Y1));
  FA fa_8 (.Cout(fa_8_cout), .F(fa_8_f), .Cin(fa_12_cout), .X(X2Y3), .Y(fa_7_f));
  FA fa_9 (.Cout(fa_9_cout), .F(fa_9_f), .Cin(fa_13_cout), .X(X1Y4), .Y(fa_8_f));
  FA fa_10 (.Cout(fa_10_cout), .F(\乘积 [5]), .Cin(fa_14_cout), .X(1'b0), .Y(fa_9_f));
  FA fa_11 (.Cout(fa_11_cout), .F(fa_11_f), .Cin(1'b0), .X(X3Y1), .Y(X4Y0));
  FA fa_12 (.Cout(fa_12_cout), .F(fa_12_f), .Cin(fa_15_cout), .X(X2Y2), .Y(fa_11_f));
  FA fa_13 (.Cout(fa_13_cout), .F(fa_13_f), .Cin(fa_16_cout), .X(X1Y3), .Y(fa_12_f));
  FA fa_14 (.Cout(fa_14_cout), .F(\乘积 [4]), .Cin(fa_17_cout), .X(X0Y4), .Y(fa_13_f));
  FA fa_15 (.Cout(fa_15_cout), .F(fa_15_f), .Cin(1'b0), .X(X2Y1), .Y(X3Y0));
  FA fa_16 (.Cout(fa_16_cout), .F(fa_16_f), .Cin(fa_18_cout), .X(X1Y2), .Y(fa_15_f));
  FA fa_17 (.Cout(fa_17_cout), .F(\乘积 [3]), .Cin(fa_19_cout), .X(X0Y3), .Y(fa_16_f));
  FA fa_18 (.Cout(fa_18_cout), .F(fa_18_f), .Cin(1'b0), .X(X1Y1), .Y(X2Y0));
  FA fa_19 (.Cout(fa_19_cout), .F(\乘积 [2]), .Cin(fa_20_cout), .X(X0Y2), .Y(fa_18_f));
  // Probe on X
  // Probe on Y
  // Probe on \乘积 
  FA fa_20 (.Cout(fa_20_cout), .F(\乘积 [1]), .Cin(1'b0), .X(X0Y1), .Y(X1Y0));
  \与门阵列  \u_与门阵列_1  (
    .XY0({X4Y0, X3Y0, X2Y0, X1Y0, \乘积 [0]}), .XY1({X4Y1, X3Y1, X2Y1, X1Y1, X0Y1}),
    .XY2({X4Y2, X3Y2, X2Y2, X1Y2, X0Y2}), .XY3({X4Y3, X3Y3, X2Y3, X1Y3, X0Y3}),
    .XY4({X4Y4, X3Y4, X2Y4, X1Y4, X0Y4}), .Y(X), .X(Y));

  // Other names for the same wires on the sheet: P[9:0] = \乘积 ; P1 = \乘积 [1]; P2 = \乘积 [2]; P3 = \乘积 [3];
  //   P4 = \乘积 [4]; P5 = \乘积 [5]; P6 = \乘积 [6]; P7 = \乘积 [7]; P8 = \乘积 [8]; P9 = \乘积 [9]; P0 = \乘积 [0];
  //   X0Y0 = \乘积 [0]; XY0[4:0] = {X4Y0, X3Y0, X2Y0, X1Y0, \乘积 [0]}; XY1[4:0] = {X4Y1, X3Y1, X2Y1, X1Y1, X0Y1};
  //   XY2[4:0] = {X4Y2, X3Y2, X2Y2, X1Y2, X0Y2}; XY3[4:0] = {X4Y3, X3Y3, X2Y3, X1Y3, X0Y3};
  //   XY4[4:0] = {X4Y4, X3Y4, X2Y4, X1Y4, X0Y4}

  // Notes on the sheet:
  //   X: pull=down
  //   Y: pull=down
  //   5位无符号阵列乘法器
  //   ×
  //   =
endmodule

module FA (
  input  Cin,
  input  X,
  input  Y,
  output Cout,
  output F
);

  wire and_1_out, and_2_out, xor_2_out;

  or or_1 (Cout, and_2_out, and_1_out);
  and and_1 (and_1_out, Cin, xor_2_out);
  and and_2 (and_2_out, X, Y);
  xor xor_1 (F, Cin, xor_2_out);
  xor xor_2 (xor_2_out, X, Y);
endmodule

module \与门阵列  (
  input  [4:0] X,
  input  [4:0] Y,
  output [4:0] XY0,
  output [4:0] XY1,
  output [4:0] XY2,
  output [4:0] XY3,
  output [4:0] XY4
);

  and and_1 (XY0[4], X[4], Y[0]);
  and and_2 (XY1[4], X[4], Y[1]);
  and and_3 (XY2[4], X[4], Y[2]);
  and and_4 (XY3[4], X[4], Y[3]);
  and and_5 (XY4[4], X[4], Y[4]);
  and and_6 (XY0[3], X[3], Y[0]);
  and and_7 (XY1[3], X[3], Y[1]);
  and and_8 (XY2[3], X[3], Y[2]);
  and and_9 (XY3[3], X[3], Y[3]);
  and and_10 (XY4[3], X[3], Y[4]);
  and and_11 (XY0[2], X[2], Y[0]);
  and and_12 (XY1[2], X[2], Y[1]);
  and and_13 (XY2[2], X[2], Y[2]);
  and and_14 (XY3[2], X[2], Y[3]);
  and and_15 (XY4[2], X[2], Y[4]);
  and and_16 (XY0[0], X[0], Y[0]);
  and and_17 (XY0[1], X[1], Y[0]);
  and and_18 (XY1[1], X[1], Y[1]);
  and and_19 (XY1[0], X[0], Y[1]);
  and and_20 (XY2[0], X[0], Y[2]);
  and and_21 (XY2[1], X[1], Y[2]);
  and and_22 (XY3[1], X[1], Y[3]);
  and and_23 (XY3[0], X[0], Y[3]);
  and and_24 (XY4[1], X[1], Y[4]);
  and and_25 (XY4[0], X[0], Y[4]);

  // Other names for the same wires on the sheet: X0Y0 = XY0[0]; X1Y0 = XY0[1]; X2Y0 = XY0[2]; X3Y0 = XY0[3];
  //   X4Y0 = XY0[4]; X0Y1 = XY1[0]; X1Y1 = XY1[1]; X2Y1 = XY1[2]; X3Y1 = XY1[3]; X4Y1 = XY1[4]; X0Y2 = XY2[0];
  //   X1Y2 = XY2[1]; X2Y2 = XY2[2]; X3Y2 = XY2[3]; X4Y2 = XY2[4]; X0Y3 = XY3[0]; X1Y3 = XY3[1]; X2Y3 = XY3[2];
  //   X3Y3 = XY3[3]; X4Y3 = XY3[4]; X0Y4 = XY4[0]; X1Y4 = XY4[1]; X2Y4 = XY4[2]; X3Y4 = XY4[3]; X4Y4 = XY4[4]
endmodule
