// Logisim project lab4思考题3.circ as structural Verilog: 5 circuits, main circuit main
module main (
  input  CLK,
  input  [7:0] X,
  input  [3:0] Y,
  input  Reset,
  output out_5,
  output [3:0] Prod,
  output NaN,
  output Divide_zero
);

  wire comparator_1_eq, comparator_1_gt, comparator_3_eq, comparator_4_eq, comparator_5_eq, LOAD, not_1_out,
       STOP, subtractor_1_bout;
  wire [0:0] not_2_out;
  wire [3:0] counter_1_q, multiplexer_3_out, multiplexer_3_out_2, multiplexer_4_out, R, R_2_q, shifter_1_out,
       subtractor_1_out;
  wire [3:1] multiplexer_1_out;
  wire [3:3] multiplexer_1_out_2;

  // Probe on R
  Subtractor #(.width(4)) subtractor_1 (
    .a(R_2_q), .b(Y), .out(subtractor_1_out), .bout(subtractor_1_bout));  // open: bin
  Multiplexer #(.width(4), .enable("false")) multiplexer_1 (
    .in0(subtractor_1_out), .in1(R_2_q), .out({multiplexer_1_out_2[3], multiplexer_1_out}),
    .sel(subtractor_1_bout));
  Hex_Digit_Display hex_digit_display_1 (.value(X[7:4]));  // open: dp
  Hex_Digit_Display hex_digit_display_2 (.value(X[3:0]));  // open: dp
  Multiplexer #(.width(4), .enable("false")) multiplexer_2 (.in0(R_2_q), .in1(shifter_1_out), .out(R), .sel(STOP));
  not not_1 (not_1_out, STOP);
  not not_2 (not_2_out[0], subtractor_1_bout);
  Hex_Digit_Display hex_digit_display_3 (.value(Y));  // open: dp
  Shifter #(.width(4), .shift("lr")) shifter_1 (.in(R_2_q), .\dist (2'b01), .out(shifter_1_out));
  Register #(.width(4), .Select("low")) R_2 (
    .D(multiplexer_3_out_2), .en(not_1_out), .Q(R_2_q), .clk(CLK), .clr(Reset));
  Multiplexer #(.width(8), .enable("false")) multiplexer_3 (
    .in0({multiplexer_1_out, Prod, not_2_out[0]}), .in1(X), .out({multiplexer_3_out_2, multiplexer_3_out}),
    .sel(LOAD));
  Hex_Digit_Display hex_digit_display_4 (.value(Prod));  // open: dp
  Register #(.width(4), .Select("low")) register_1 (
    .D(multiplexer_3_out), .en(not_1_out), .Q(Prod), .clk(CLK), .clr(Reset));
  // Probe on Prod
  Register #(.width(4), .Select("low")) u_Y (.D(multiplexer_4_out), .en(not_1_out), .clk(CLK), .clr(Reset));  // open: Q
  Multiplexer #(.width(4), .enable("false")) multiplexer_4 (.in1(Y), .out(multiplexer_4_out), .sel(LOAD));  // open: in0
  // Probe on X
  // Probe on Y
  // Probe on Prod
  // Probe on R
  Counter #(.width(4), .max('hf)) counter_1 (
    .count(not_1_out), .Q(counter_1_q), .clk(CLK), .clr(Reset));  // open: load, D, carry, preset, down
  or or_1 (out_5, comparator_1_gt, comparator_1_eq);
  Comparator #(.width(4), .mode("unsigned")) comparator_1 (
    .a(X[7:4]), .b(Y), .gt(comparator_1_gt), .eq(comparator_1_eq));  // open: lt
  and and_1 (NaN, comparator_4_eq, comparator_5_eq);
  Comparator #(.width(4)) comparator_2 (.a(counter_1_q), .b(4'b0000), .eq(LOAD));  // open: gt, lt
  Comparator #(.width(4)) comparator_3 (.a(counter_1_q), .b(4'b0110), .eq(comparator_3_eq));  // open: gt, lt
  Comparator #(.mode("unsigned")) comparator_4 (.a(X), .b({8{1'b0}}), .eq(comparator_4_eq));  // open: gt, lt
  and and_2 (Divide_zero, ~comparator_4_eq, comparator_5_eq);  // AND_Gate
  Comparator #(.width(4), .mode("unsigned")) comparator_5 (.a(Y), .b(4'b0000), .eq(comparator_5_eq));  // open: gt, lt
  or or_2 (STOP, comparator_3_eq, NaN, Divide_zero);

  // Other names for the same wires on the sheet: Overflow = out_5; Q[3:0] = Prod; RST = Reset

  // Notes on the sheet:
  //   输入引脚
  //   ÷
  //   =
  //   请勿修改引脚名称、电路名称及电路封装外观
  //   Q
  //   ÷
  //   =
  //   输出引脚
endmodule

module CNTR4U (
  input  CLK,
  input  LD,
  input  CLR,
  input  D0,
  input  D1,
  input  D2,
  input  D3,
  input  ENP,
  input  ENT,
  output Q0,
  output Q1,
  output Q2,
  output Q3,
  output RCO
);

  wire and_1_out, and_2_out, and_3_out, and_4_out, and_5_out, and_6_out, and_7_out, and_8_out, and_10_out,
       and_11_out, and_12_out, and_13_out, and_14_out, and_15_out, and_16_out, and_17_out, buffer_1_out,
       d_ff_1_qn, d_ff_2_qn, d_ff_3_qn, d_ff_4_qn, not_1_out, not_2_out, or_1_out, or_2_out, or_3_out,
       or_4_out, xor_1_out, xor_2_out, xor_3_out, xor_4_out;

  buf buffer_1 (buffer_1_out, CLR);
  and and_1 (and_1_out, ENP, ENT);
  not not_1 (not_1_out, CLK);
  and and_2 (and_2_out, ~d_ff_2_qn, ~d_ff_1_qn);  // AND_Gate
  and and_3 (and_3_out, ~d_ff_3_qn, ~d_ff_2_qn, ~d_ff_1_qn);  // AND_Gate
  not not_2 (not_2_out, ENT);
  xor xor_1 (xor_1_out, and_1_out, ~d_ff_1_qn);  // XOR_Gate
  and and_4 (and_4_out, ~d_ff_1_qn, and_1_out);  // AND_Gate
  and and_5 (and_5_out, and_2_out, and_1_out);
  and and_6 (and_6_out, and_3_out, and_1_out);
  and and_7 (and_7_out, LD, ~buffer_1_out);  // AND_Gate
  and and_8 (and_8_out, ~and_7_out, ~buffer_1_out);  // AND_Gate
  xor xor_2 (xor_2_out, and_4_out, ~d_ff_2_qn);  // XOR_Gate
  xor xor_3 (xor_3_out, and_5_out, ~d_ff_3_qn);  // XOR_Gate
  xor xor_4 (xor_4_out, and_6_out, ~d_ff_4_qn);  // XOR_Gate
  and and_9 (RCO, ~d_ff_4_qn, ~d_ff_3_qn, ~d_ff_2_qn, ~d_ff_1_qn, ~not_2_out);  // AND_Gate
  and and_10 (and_10_out, and_7_out, D0);
  or or_1 (or_1_out, and_10_out, and_11_out);
  and and_11 (and_11_out, and_8_out, xor_1_out);
  and and_12 (and_12_out, and_7_out, D1);
  or or_2 (or_2_out, and_12_out, and_13_out);
  and and_13 (and_13_out, and_8_out, xor_2_out);
  and and_14 (and_14_out, and_7_out, D2);
  or or_3 (or_3_out, and_14_out, and_15_out);
  and and_15 (and_15_out, and_8_out, xor_3_out);
  and and_16 (and_16_out, and_7_out, D3);
  or or_4 (or_4_out, and_16_out, and_17_out);
  and and_17 (and_17_out, and_8_out, xor_4_out);
  D_Flip_Flop #(.trigger("falling")) d_ff_1 (
    .clk(not_1_out), .D(or_1_out), .Q(Q0), .Qn(d_ff_1_qn));  // open: preset, reset
  D_Flip_Flop #(.trigger("falling")) d_ff_2 (
    .clk(not_1_out), .D(or_2_out), .Q(Q1), .Qn(d_ff_2_qn));  // open: preset, reset
  D_Flip_Flop #(.trigger("falling")) d_ff_3 (
    .clk(not_1_out), .D(or_3_out), .Q(Q2), .Qn(d_ff_3_qn));  // open: preset, reset
  D_Flip_Flop #(.trigger("falling")) d_ff_4 (
    .clk(not_1_out), .D(or_4_out), .Q(Q3), .Qn(d_ff_4_qn));  // open: preset, reset

  // Notes on the sheet:
  //   输入引脚
  //   提示：使用独立逻辑门实现4位二进制同步计数器，禁止直接使用计数器组件。
  //   请勿修改引脚名称、电路名称及电路封装外观
  //   输出引脚
endmodule

module ADDER4b (
  input  [3:0] X,
  input  [3:0] Y,
  input  Cin,
  output [3:0] F,
  output Cout
);

  wire fa_1_cout, fa_2_cout, fa_3_cout;
  wire [3:0] bit_extender_1_out, xor_1_out;

  assign bit_extender_1_out = {{3{Cin}}, Cin};  // Bit_Extender bit_extender_1
  Hex_Digit_Display hex_digit_display_1 (.value(X), .dp(1'b0));
  assign xor_1_out = bit_extender_1_out ^ Y;  // XOR_Gate xor_1, 4 bits wide
  Hex_Digit_Display hex_digit_display_2 (.value(xor_1_out), .dp(1'b0));
  FA fa_1 (.A(X[0]), .B(xor_1_out[0]), .Cin(Cin), .F(F[0]), .Cout(fa_1_cout));
  Hex_Digit_Display hex_digit_display_3 (.value(F), .dp(1'b0));
  FA fa_2 (.A(X[1]), .B(xor_1_out[1]), .Cin(fa_1_cout), .F(F[1]), .Cout(fa_2_cout));
  FA fa_3 (.A(X[2]), .B(xor_1_out[2]), .Cin(fa_2_cout), .F(F[2]), .Cout(fa_3_cout));
  FA fa_4 (.A(X[3]), .B(xor_1_out[3]), .Cin(fa_3_cout), .F(F[3]), .Cout(Cout));

  // Other names for the same wires on the sheet: SUM[3:0] = F; 操作数x[3:0] = X; 操作数y[3:0] = Y

  // Notes on the sheet:
  //   输入引脚
  //   +
  //   =
  //   请勿修改引脚名称、电路名称及电路封装外观
  //   提示：使用独立逻辑门及全加器FA子电路实现4位二进制数加减法器，禁止直接使用加减法器组件。
  //   输出引脚
endmodule

module FA (
  input  A,
  input  B,
  input  Cin,
  output F,
  output Cout
);

  wire and_1_out, and_2_out, and_3_out;

  xor xor_1 (F, A, B, Cin);
  and and_1 (and_1_out, A, B);
  and and_2 (and_2_out, B, Cin);
  and and_3 (and_3_out, A, Cin);
  or or_1 (Cout, and_1_out, and_2_out, and_3_out);

  // Notes on the sheet:
  //   全加器
endmodule

module BarrelSFT8b (
  input  [7:0] DataIn,
  input  [2:0] shamt,
  input  L_R,
  input  A_L,
  input  IN,
  output [7:0] DataOut
);

  wire and_1_out;
  wire [0:0] multiplexer_2_out;
  wire [1:0] multiplexer_4_out;
  wire [3:0] multiplexer_5_out_2, multiplexer_6_out;
  wire [7:0] multiplexer_3_out;
  wire [7:4] multiplexer_5_out;
  wire [7:7] multiplexer_1_out;

  and and_1 (and_1_out, L_R, A_L);
  Multiplexer #(.enable("false")) multiplexer_1 (.in0(1'b0), .in1(DataIn[7]), .out(multiplexer_1_out[7]), .sel(A_L));
  Multiplexer #(.enable("false")) multiplexer_2 (
    .in0(1'b0), .in1(DataIn[7]), .out(multiplexer_2_out[0]), .sel(and_1_out));
  Multiplexer #(.select(2), .width(8), .enable("false")) multiplexer_3 (
    .in0(DataIn), .in1({multiplexer_1_out[7], DataIn[7:1]}), .in2(DataIn),
    .in3({DataIn[6:0], multiplexer_2_out[0]}), .out(multiplexer_3_out), .sel({L_R, shamt[0]}));
  Multiplexer #(.width(2), .enable("false")) multiplexer_4 (
    .in0(2'b00), .in1(multiplexer_3_out[7:6]), .out(multiplexer_4_out), .sel(and_1_out));
  Multiplexer #(.select(2), .width(8), .enable("false")) multiplexer_5 (
    .in0(multiplexer_3_out), .in1({{2{multiplexer_1_out[7]}}, multiplexer_3_out[7:2]}),
    .in2(multiplexer_3_out), .in3({multiplexer_3_out[5:0], multiplexer_4_out}),
    .out({multiplexer_5_out, multiplexer_5_out_2}), .sel({L_R, shamt[1]}));
  Multiplexer #(.width(4), .enable("false")) multiplexer_6 (
    .in0(4'b0000), .in1(multiplexer_5_out), .out(multiplexer_6_out), .sel(and_1_out));
  Multiplexer #(.select(2), .width(8), .enable("false")) multiplexer_7 (
    .in0({multiplexer_5_out, multiplexer_5_out_2}), .in1({{4{multiplexer_1_out[7]}}, multiplexer_5_out}),
    .in2({multiplexer_5_out, multiplexer_5_out_2}), .in3({multiplexer_5_out_2, multiplexer_6_out}),
    .out(DataOut), .sel({L_R, shamt[2]}));

  // Other names for the same wires on the sheet: Din[7:0] = DataIn; Left_Right = L_R; Arth_Logic = A_L;
  //   Dout[7:0] = DataOut; Input = IN

  // Notes on the sheet:
  //   L/R,A/L: 00逻辑右移，01算术右移，10逻辑左移，11：循环左移
  //   输入引脚
  //   请勿修改引脚名称、电路名称及电路封装外观
  //   提示：使用多路选择器级联实现8位桶形移位器，禁止直接使用移位器组件。
  //   输出引脚
endmodule
