// Logisim project lab5.1.circ as structural Verilog: 1 circuit, main circuit main
// ASCII-ZK
module main (
  input  [6:0] ASCII_CODE,
  output [7:0] row1,
  output [7:0] row2,
  output [7:0] row3,
  output [7:0] row4,
  output [7:0] row5,
  output [7:0] row6,
  output [7:0] row7,
  output [7:0] row8,
  output [7:0] row9,
  output [7:0] row10,
  output [7:0] row11,
  output [7:0] row12,
  output [7:0] row13,
  output [7:0] row14,
  output [7:0] row15,
  output [7:0] row16,
  output CodeErr
);

  wire comparator_1_lt, comparator_2_gt, not_1_out;
  wire [15:0] adder_1_out, adder_2_out, adder_3_out, adder_4_out, adder_5_out, adder_6_out, adder_7_out,
       adder_8_out, adder_9_out, adder_10_out, adder_11_out, adder_12_out, adder_13_out, adder_14_out,
       adder_15_out, bit_extender_1_out, shifter_1_out, subtractor_1_out;

  or or_1 (CodeErr, comparator_1_lt, comparator_2_gt);
  Subtractor #(.width(16)) subtractor_1 (
    .a(bit_extender_1_out), .b(16'h20), .out(subtractor_1_out));  // open: bin, bout
  assign bit_extender_1_out = {{9{1'b0}}, ASCII_CODE};  // Bit_Extender bit_extender_1
  not not_1 (not_1_out, CodeErr);
  Comparator #(.width(16), .mode("unsigned")) comparator_1 (
    .a(bit_extender_1_out), .b(16'h20), .lt(comparator_1_lt));  // open: gt, eq
  Comparator #(.width(16), .mode("unsigned")) comparator_2 (
    .a(bit_extender_1_out), .b(16'h7f), .gt(comparator_2_gt));  // open: eq, lt
  Shifter #(.width(16)) shifter_1 (.in(subtractor_1_out), .\dist (4'b0100), .out(shifter_1_out));
  Adder #(.width(16)) adder_1 (.a(shifter_1_out), .b(16'h2), .out(adder_1_out));  // open: cin, cout
  Adder #(.width(16)) adder_2 (.a(shifter_1_out), .b(16'h4), .out(adder_2_out));  // open: cin, cout
  Adder #(.width(16)) adder_3 (.a(shifter_1_out), .b(16'h6), .out(adder_3_out));  // open: cin, cout
  Adder #(.width(16)) adder_4 (.a(shifter_1_out), .b(16'h8), .out(adder_4_out));  // open: cin, cout
  Adder #(.width(16)) adder_5 (.a(shifter_1_out), .b(16'ha), .out(adder_5_out));  // open: cin, cout
  Adder #(.width(16)) adder_6 (.a(shifter_1_out), .b(16'hc), .out(adder_6_out));  // open: cin, cout
  Adder #(.width(16)) adder_7 (.a(shifter_1_out), .b(16'he), .out(adder_7_out));  // open: cin, cout
  ROM #(.addrWidth(16), .Select("high"), .simpleMode("false")) rom_1 (
    .addr(shifter_1_out), .data(row1), .sel(not_1_out));
  ROM #(.addrWidth(16), .Select("high")) rom_2 (.addr(adder_1_out), .data(row3), .sel(not_1_out));
  ROM #(.addrWidth(16), .Select("high")) rom_3 (.addr(adder_2_out), .data(row5), .sel(not_1_out));
  ROM #(.addrWidth(16), .Select("high")) rom_4 (.addr(adder_3_out), .data(row7), .sel(not_1_out));
  ROM #(.addrWidth(16), .Select("high")) rom_5 (.addr(adder_4_out), .data(row9), .sel(not_1_out));
  ROM #(.addrWidth(16), .Select("high")) rom_6 (.addr(adder_5_out), .data(row11), .sel(not_1_out));
  ROM #(.addrWidth(16), .Select("high")) rom_7 (.addr(adder_6_out), .data(row13), .sel(not_1_out));
  ROM #(.addrWidth(16), .Select("high")) rom_8 (.addr(adder_7_out), .data(row15), .sel(not_1_out));
  Adder #(.width(16)) adder_8 (.a(shifter_1_out), .b(16'h1), .out(adder_8_out));  // open: cin, cout
  Adder #(.width(16)) adder_9 (.a(shifter_1_out), .b(16'h3), .out(adder_9_out));  // open: cin, cout
  Adder #(.width(16)) adder_10 (.a(shifter_1_out), .b(16'h5), .out(adder_10_out));  // open: cin, cout
  Adder #(.width(16)) adder_11 (.a(shifter_1_out), .b(16'h7), .out(adder_11_out));  // open: cin, cout
  Adder #(.width(16)) adder_12 (.a(shifter_1_out), .b(16'h9), .out(adder_12_out));  // open: cin, cout
  Adder #(.width(16)) adder_13 (.a(shifter_1_out), .b(16'hb), .out(adder_13_out));  // open: cin, cout
  Adder #(.width(16)) adder_14 (.a(shifter_1_out), .b(16'hd), .out(adder_14_out));  // open: cin, cout
  Adder #(.width(16)) adder_15 (.a(shifter_1_out), .b(16'hf), .out(adder_15_out));  // open: cin, cout
  ROM #(.addrWidth(16), .Select("high")) rom_9 (.addr(adder_8_out), .data(row2), .sel(not_1_out));
  ROM #(.addrWidth(16), .Select("high")) rom_10 (.addr(adder_9_out), .data(row4), .sel(not_1_out));
  ROM #(.addrWidth(16), .Select("high")) rom_11 (.addr(adder_10_out), .data(row6), .sel(not_1_out));
  ROM #(.addrWidth(16), .Select("high")) rom_12 (.addr(adder_11_out), .data(row8), .sel(not_1_out));
  ROM #(.addrWidth(16), .Select("high")) rom_13 (.addr(adder_12_out), .data(row10), .sel(not_1_out));
  ROM #(.addrWidth(16), .Select("high")) rom_14 (.addr(adder_13_out), .data(row12), .sel(not_1_out));
  ROM #(.addrWidth(16), .Select("high")) rom_15 (.addr(adder_14_out), .data(row14), .sel(not_1_out));
  ROM #(.addrWidth(16), .Select("high")) rom_16 (.addr(adder_15_out), .data(row16), .sel(not_1_out));
  DotMatrix #(.inputtype("row"), .matrixcols(8), .matrixrows(16)) dotmatrix_1 (
    .row0(row1), .row1(row2), .row2(row3), .row3(row4), .row4(row5), .row5(row6), .row6(row7), .row7(row8),
    .row8(row9), .row9(row10), .row10(row11), .row11(row12), .row12(row13), .row13(row14), .row14(row15),
    .row15(row16));

  // Other names for the same wires on the sheet: Code[6:0] = ASCII_CODE

  // Notes on the sheet:
  //   ASCII编码
  //   输入引脚
  //   请勿修改引脚名称、电路名称及电路封装外观
  //   contents of rom_1 (hex, n*v repeats v):
  //   18*0 18 3c 3c 3c 18 18 18 0 18 18 5*0 63 63 63 22 14*0 36 36 7f 36 36 36 7f 36 36 4*0 c c 3e 63 61
  //   60 3e 3 3 43 63 3e c c 7*0 61 63 6 c 18 33 63 7*0 1c 36 36 1c 3b 6e 66 66 3b 5*0 30 30 30 60 13*0 c
  //   18 18 4*30 18 18 c 6*0 18 c c 4*6 c c 18 8*0 42 66 3c ff 3c 66 42 9*0 18 18 18 ff 18 18 18 15*0 18
  //   18 18 30 9*0 ff 18*0 18 18 6*0 1 3 7 e 1c 38 70 e0 c0 80 6*0 3e 63 63 63 6b 6b 63 63 63 3e 6*0 c 1c
  //   3c 6*c 3f 6*0 3e 63 3 6 c 18 30 61 63 7f 6*0 3e 63 3 3 1e 3 3 3 63 3e 6*0 6 e 1e 36 66 66 7f 6 6 f
  //   6*0 7f 60 60 60 7e 3 3 63 73 3e 6*0 1c 30 60 60 7e 4*63 3e 6*0 7f 63 3 6 6 c c 18 18 18 6*0 3e 63 63
  //   63 3e 4*63 3e 6*0 3e 4*63 3f 3 3 6 3c 9*0 18 18 0 0 0 18 18 9*0 18 18 0 0 0 18 18 18 30 5*0 6 c 18
  //   30 60 30 18 c 6 10*0 7e 0 0 7e 9*0 60 30 18 c 6 c 18 30 60 6*0 3e 63 63 6 c c c 0 c c 6*0 3e 63 63
  //   6f 6b 6b 6e 60 60 3e 6*0 8 1c 36 63 63 63 7f 63 63 63 6*0 7e 33 33 33 3e 4*33 7e 6*0 1e 33 61 4*60
  //   61 33 1e 6*0 7c 36 6*33 36 7c 6*0 7f 33 31 34 3c 34 30 31 33 7f 6*0 7f 33 31 34 3c 34 30 30 30 78
  //   6*0 1e 33 61 60 60 6f 63 63 37 1d 6*0 4*63 7f 5*63 6*0 3c 8*18 3c 6*0 f 6*6 66 66 3c 6*0 73 33 36 36
  //   3c 36 36 33 33 73 6*0 78 6*30 31 33 7f 6*0 63 77 7f 6b 6*63 6*0 63 63 73 7b 7f 6f 67 63 63 63 6*0 1c
  //   36 6*63 36 1c 6*0 7e 33 33 33 3e 4*30 78 6*0 3e 6*63 6b 6f 3e 6 7 4*0 7e 33 33 33 3e 36 36 33 33 73
  //   6*0 3e 63 63 30 1c 6 3 63 63 3e 6*0 ff db 99 6*18 3c 6*0 9*63 3e 6*0 7*63 36 1c 8 6*0 5*63 6b 6b 7f
  //   36 36 6*0 c3 c3 66 3c 18 18 3c 66 c3 c3 6*0 c3 c3 c3 66 3c 4*18 3c 6*0 7f 63 43 6 c 18 30 61 63 7f
  //   6*0 3c 8*30 3c 6*0 80 c0 e0 70 38 1c e 7 3 1 6*0 3c 8*c 3c 4*0 8 1c 36 63 24*0 ff 0 0 0 18 18 c 18*0
  //   3c 46 6 3e 66 66 3b 6*0 70 30 30 3c 36 4*33 6e 9*0 3e 63 60 60 60 63 3e 6*0 e 6 6 1e 36 4*66 3b 9*0
  //   3e 63 63 7e 60 63 3e 6*0 1c 36 32 30 7c 4*30 78 9*0 3b 4*66 3e 6 66 3c 4*0 70 30 30 36 3b 4*33 73
  //   6*0 c c 0 1c 5*c 1e 6*0 6 6 0 e 5*6 66 66 3c 4*0 70 30 30 33 33 36 3c 36 33 73 6*0 1c 8*c 1e 9*0 6e
  //   7f 5*6b 9*0 6e 6*33 9*0 3e 5*63 3e 9*0 6e 4*33 3e 30 30 78 7*0 3b 4*66 3e 6 6 f 7*0 6e 3b 33 30 30
  //   30 78 9*0 3e 63 38 e 3 63 3e 6*0 8 18 18 7e 4*18 1b e 9*0 6*66 3b 9*0 63 63 36 36 1c 1c 8 9*0 63 63
  //   63 6b 6b 7f 36 9*0 63 36 1c 1c 1c 36 63 9*0 5*63 3f 3 6 3c 7*0 7f 66 c 18 30 63 7f 6*0 e 18 18 18 70
  //   4*18 e 6*0 5*18 0 5*18 5*0 70 18 18 18 e 4*18 70 6*0 3b 6e 13*0 70 d8 d8 70
  //   contents of rom_2 (hex, n*v repeats v):
  //   18*0 18 3c 3c 3c 18 18 18 0 18 18 5*0 63 63 63 22 14*0 36 36 7f 36 36 36 7f 36 36 4*0 c c 3e 63 61
  //   60 3e 3 3 43 63 3e c c 7*0 61 63 6 c 18 33 63 7*0 1c 36 36 1c 3b 6e 66 66 3b 5*0 30 30 30 60 13*0 c
  //   18 18 4*30 18 18 c 6*0 18 c c 4*6 c c 18 8*0 42 66 3c ff 3c 66 42 9*0 18 18 18 ff 18 18 18 15*0 18
  //   18 18 30 9*0 ff 18*0 18 18 6*0 1 3 7 e 1c 38 70 e0 c0 80 6*0 3e 63 63 63 6b 6b 63 63 63 3e 6*0 c 1c
  //   3c 6*c 3f 6*0 3e 63 3 6 c 18 30 61 63 7f 6*0 3e 63 3 3 1e 3 3 3 63 3e 6*0 6 e 1e 36 66 66 7f 6 6 f
  //   6*0 7f 60 60 60 7e 3 3 63 73 3e 6*0 1c 30 60 60 7e 4*63 3e 6*0 7f 63 3 6 6 c c 18 18 18 6*0 3e 63 63
  //   63 3e 4*63 3e 6*0 3e 4*63 3f 3 3 6 3c 9*0 18 18 0 0 0 18 18 9*0 18 18 0 0 0 18 18 18 30 5*0 6 c 18
  //   30 60 30 18 c 6 10*0 7e 0 0 7e 9*0 60 30 18 c 6 c 18 30 60 6*0 3e 63 63 6 c c c 0 c c 6*0 3e 63 63
  //   6f 6b 6b 6e 60 60 3e 6*0 8 1c 36 63 63 63 7f 63 63 63 6*0 7e 33 33 33 3e 4*33 7e 6*0 1e 33 61 4*60
  //   61 33 1e 6*0 7c 36 6*33 36 7c 6*0 7f 33 31 34 3c 34 30 31 33 7f 6*0 7f 33 31 34 3c 34 30 30 30 78
  //   6*0 1e 33 61 60 60 6f 63 63 37 1d 6*0 4*63 7f 5*63 6*0 3c 8*18 3c 6*0 f 6*6 66 66 3c 6*0 73 33 36 36
  //   3c 36 36 33 33 73 6*0 78 6*30 31 33 7f 6*0 63 77 7f 6b 6*63 6*0 63 63 73 7b 7f 6f 67 63 63 63 6*0 1c
  //   36 6*63 36 1c 6*0 7e 33 33 33 3e 4*30 78 6*0 3e 6*63 6b 6f 3e 6 7 4*0 7e 33 33 33 3e 36 36 33 33 73
  //   6*0 3e 63 63 30 1c 6 3 63 63 3e 6*0 ff db 99 6*18 3c 6*0 9*63 3e 6*0 7*63 36 1c 8 6*0 5*63 6b 6b 7f
  //   36 36 6*0 c3 c3 66 3c 18 18 3c 66 c3 c3 6*0 c3 c3 c3 66 3c 4*18 3c 6*0 7f 63 43 6 c 18 30 61 63 7f
  //   6*0 3c 8*30 3c 6*0 80 c0 e0 70 38 1c e 7 3 1 6*0 3c 8*c 3c 4*0 8 1c 36 63 24*0 ff 0 0 0 18 18 c 18*0
  //   3c 46 6 3e 66 66 3b 6*0 70 30 30 3c 36 4*33 6e 9*0 3e 63 60 60 60 63 3e 6*0 e 6 6 1e 36 4*66 3b 9*0
  //   3e 63 63 7e 60 63 3e 6*0 1c 36 32 30 7c 4*30 78 9*0 3b 4*66 3e 6 66 3c 4*0 70 30 30 36 3b 4*33 73
  //   6*0 c c 0 1c 5*c 1e 6*0 6 6 0 e 5*6 66 66 3c 4*0 70 30 30 33 33 36 3c 36 33 73 6*0 1c 8*c 1e 9*0 6e
  //   7f 5*6b 9*0 6e 6*33 9*0 3e 5*63 3e 9*0 6e 4*33 3e 30 30 78 7*0 3b 4*66 3e 6 6 f 7*0 6e 3b 33 30 30
  //   30 78 9*0 3e 63 38 e 3 63 3e 6*0 8 18 18 7e 4*18 1b e 9*0 6*66 3b 9*0 63 63 36 36 1c 1c 8 9*0 63 63
  //   63 6b 6b 7f 36 9*0 63 36 1c 1c 1c 36 63 9*0 5*63 3f 3 6 3c 7*0 7f 66 c 18 30 63 7f 6*0 e 18 18 18 70
  //   4*18 e 6*0 5*18 0 5*18 5*0 70 18 18 18 e 4*18 70 6*0 3b 6e 13*0 70 d8 d8 70
  //   contents of rom_3 (hex, n*v repeats v):
  //   18*0 18 3c 3c 3c 18 18 18 0 18 18 5*0 63 63 63 22 14*0 36 36 7f 36 36 36 7f 36 36 4*0 c c 3e 63 61
  //   60 3e 3 3 43 63 3e c c 7*0 61 63 6 c 18 33 63 7*0 1c 36 36 1c 3b 6e 66 66 3b 5*0 30 30 30 60 13*0 c
  //   18 18 4*30 18 18 c 6*0 18 c c 4*6 c c 18 8*0 42 66 3c ff 3c 66 42 9*0 18 18 18 ff 18 18 18 15*0 18
  //   18 18 30 9*0 ff 18*0 18 18 6*0 1 3 7 e 1c 38 70 e0 c0 80 6*0 3e 63 63 63 6b 6b 63 63 63 3e 6*0 c 1c
  //   3c 6*c 3f 6*0 3e 63 3 6 c 18 30 61 63 7f 6*0 3e 63 3 3 1e 3 3 3 63 3e 6*0 6 e 1e 36 66 66 7f 6 6 f
  //   6*0 7f 60 60 60 7e 3 3 63 73 3e 6*0 1c 30 60 60 7e 4*63 3e 6*0 7f 63 3 6 6 c c 18 18 18 6*0 3e 63 63
  //   63 3e 4*63 3e 6*0 3e 4*63 3f 3 3 6 3c 9*0 18 18 0 0 0 18 18 9*0 18 18 0 0 0 18 18 18 30 5*0 6 c 18
  //   30 60 30 18 c 6 10*0 7e 0 0 7e 9*0 60 30 18 c 6 c 18 30 60 6*0 3e 63 63 6 c c c 0 c c 6*0 3e 63 63
  //   6f 6b 6b 6e 60 60 3e 6*0 8 1c 36 63 63 63 7f 63 63 63 6*0 7e 33 33 33 3e 4*33 7e 6*0 1e 33 61 4*60
  //   61 33 1e 6*0 7c 36 6*33 36 7c 6*0 7f 33 31 34 3c 34 30 31 33 7f 6*0 7f 33 31 34 3c 34 30 30 30 78
  //   6*0 1e 33 61 60 60 6f 63 63 37 1d 6*0 4*63 7f 5*63 6*0 3c 8*18 3c 6*0 f 6*6 66 66 3c 6*0 73 33 36 36
  //   3c 36 36 33 33 73 6*0 78 6*30 31 33 7f 6*0 63 77 7f 6b 6*63 6*0 63 63 73 7b 7f 6f 67 63 63 63 6*0 1c
  //   36 6*63 36 1c 6*0 7e 33 33 33 3e 4*30 78 6*0 3e 6*63 6b 6f 3e 6 7 4*0 7e 33 33 33 3e 36 36 33 33 73
  //   6*0 3e 63 63 30 1c 6 3 63 63 3e 6*0 ff db 99 6*18 3c 6*0 9*63 3e 6*0 7*63 36 1c 8 6*0 5*63 6b 6b 7f
  //   36 36 6*0 c3 c3 66 3c 18 18 3c 66 c3 c3 6*0 c3 c3 c3 66 3c 4*18 3c 6*0 7f 63 43 6 c 18 30 61 63 7f
  //   6*0 3c 8*30 3c 6*0 80 c0 e0 70 38 1c e 7 3 1 6*0 3c 8*c 3c 4*0 8 1c 36 63 24*0 ff 0 0 0 18 18 c 18*0
  //   3c 46 6 3e 66 66 3b 6*0 70 30 30 3c 36 4*33 6e 9*0 3e 63 60 60 60 63 3e 6*0 e 6 6 1e 36 4*66 3b 9*0
  //   3e 63 63 7e 60 63 3e 6*0 1c 36 32 30 7c 4*30 78 9*0 3b 4*66 3e 6 66 3c 4*0 70 30 30 36 3b 4*33 73
  //   6*0 c c 0 1c 5*c 1e 6*0 6 6 0 e 5*6 66 66 3c 4*0 70 30 30 33 33 36 3c 36 33 73 6*0 1c 8*c 1e 9*0 6e
  //   7f 5*6b 9*0 6e 6*33 9*0 3e 5*63 3e 9*0 6e 4*33 3e 30 30 78 7*0 3b 4*66 3e 6 6 f 7*0 6e 3b 33 30 30
  //   30 78 9*0 3e 63 38 e 3 63 3e 6*0 8 18 18 7e 4*18 1b e 9*0 6*66 3b 9*0 63 63 36 36 1c 1c 8 9*0 63 63
  //   63 6b 6b 7f 36 9*0 63 36 1c 1c 1c 36 63 9*0 5*63 3f 3 6 3c 7*0 7f 66 c 18 30 63 7f 6*0 e 18 18 18 70
  //   4*18 e 6*0 5*18 0 5*18 5*0 70 18 18 18 e 4*18 70 6*0 3b 6e 13*0 70 d8 d8 70
  //   contents of rom_4 (hex, n*v repeats v):
  //   18*0 18 3c 3c 3c 18 18 18 0 18 18 5*0 63 63 63 22 14*0 36 36 7f 36 36 36 7f 36 36 4*0 c c 3e 63 61
  //   60 3e 3 3 43 63 3e c c 7*0 61 63 6 c 18 33 63 7*0 1c 36 36 1c 3b 6e 66 66 3b 5*0 30 30 30 60 13*0 c
  //   18 18 4*30 18 18 c 6*0 18 c c 4*6 c c 18 8*0 42 66 3c ff 3c 66 42 9*0 18 18 18 ff 18 18 18 15*0 18
  //   18 18 30 9*0 ff 18*0 18 18 6*0 1 3 7 e 1c 38 70 e0 c0 80 6*0 3e 63 63 63 6b 6b 63 63 63 3e 6*0 c 1c
  //   3c 6*c 3f 6*0 3e 63 3 6 c 18 30 61 63 7f 6*0 3e 63 3 3 1e 3 3 3 63 3e 6*0 6 e 1e 36 66 66 7f 6 6 f
  //   6*0 7f 60 60 60 7e 3 3 63 73 3e 6*0 1c 30 60 60 7e 4*63 3e 6*0 7f 63 3 6 6 c c 18 18 18 6*0 3e 63 63
  //   63 3e 4*63 3e 6*0 3e 4*63 3f 3 3 6 3c 9*0 18 18 0 0 0 18 18 9*0 18 18 0 0 0 18 18 18 30 5*0 6 c 18
  //   30 60 30 18 c 6 10*0 7e 0 0 7e 9*0 60 30 18 c 6 c 18 30 60 6*0 3e 63 63 6 c c c 0 c c 6*0 3e 63 63
  //   6f 6b 6b 6e 60 60 3e 6*0 8 1c 36 63 63 63 7f 63 63 63 6*0 7e 33 33 33 3e 4*33 7e 6*0 1e 33 61 4*60
  //   61 33 1e 6*0 7c 36 6*33 36 7c 6*0 7f 33 31 34 3c 34 30 31 33 7f 6*0 7f 33 31 34 3c 34 30 30 30 78
  //   6*0 1e 33 61 60 60 6f 63 63 37 1d 6*0 4*63 7f 5*63 6*0 3c 8*18 3c 6*0 f 6*6 66 66 3c 6*0 73 33 36 36
  //   3c 36 36 33 33 73 6*0 78 6*30 31 33 7f 6*0 63 77 7f 6b 6*63 6*0 63 63 73 7b 7f 6f 67 63 63 63 6*0 1c
  //   36 6*63 36 1c 6*0 7e 33 33 33 3e 4*30 78 6*0 3e 6*63 6b 6f 3e 6 7 4*0 7e 33 33 33 3e 36 36 33 33 73
  //   6*0 3e 63 63 30 1c 6 3 63 63 3e 6*0 ff db 99 6*18 3c 6*0 9*63 3e 6*0 7*63 36 1c 8 6*0 5*63 6b 6b 7f
  //   36 36 6*0 c3 c3 66 3c 18 18 3c 66 c3 c3 6*0 c3 c3 c3 66 3c 4*18 3c 6*0 7f 63 43 6 c 18 30 61 63 7f
  //   6*0 3c 8*30 3c 6*0 80 c0 e0 70 38 1c e 7 3 1 6*0 3c 8*c 3c 4*0 8 1c 36 63 24*0 ff 0 0 0 18 18 c 18*0
  //   3c 46 6 3e 66 66 3b 6*0 70 30 30 3c 36 4*33 6e 9*0 3e 63 60 60 60 63 3e 6*0 e 6 6 1e 36 4*66 3b 9*0
  //   3e 63 63 7e 60 63 3e 6*0 1c 36 32 30 7c 4*30 78 9*0 3b 4*66 3e 6 66 3c 4*0 70 30 30 36 3b 4*33 73
  //   6*0 c c 0 1c 5*c 1e 6*0 6 6 0 e 5*6 66 66 3c 4*0 70 30 30 33 33 36 3c 36 33 73 6*0 1c 8*c 1e 9*0 6e
  //   7f 5*6b 9*0 6e 6*33 9*0 3e 5*63 3e 9*0 6e 4*33 3e 30 30 78 7*0 3b 4*66 3e 6 6 f 7*0 6e 3b 33 30 30
  //   30 78 9*0 3e 63 38 e 3 63 3e 6*0 8 18 18 7e 4*18 1b e 9*0 6*66 3b 9*0 63 63 36 36 1c 1c 8 9*0 63 63
  //   63 6b 6b 7f 36 9*0 63 36 1c 1c 1c 36 63 9*0 5*63 3f 3 6 3c 7*0 7f 66 c 18 30 63 7f 6*0 e 18 18 18 70
  //   4*18 e 6*0 5*18 0 5*18 5*0 70 18 18 18 e 4*18 70 6*0 3b 6e 13*0 70 d8 d8 70
  //   contents of rom_5 (hex, n*v repeats v):
  //   18*0 18 3c 3c 3c 18 18 18 0 18 18 5*0 63 63 63 22 14*0 36 36 7f 36 36 36 7f 36 36 4*0 c c 3e 63 61
  //   60 3e 3 3 43 63 3e c c 7*0 61 63 6 c 18 33 63 7*0 1c 36 36 1c 3b 6e 66 66 3b 5*0 30 30 30 60 13*0 c
  //   18 18 4*30 18 18 c 6*0 18 c c 4*6 c c 18 8*0 42 66 3c ff 3c 66 42 9*0 18 18 18 ff 18 18 18 15*0 18
  //   18 18 30 9*0 ff 18*0 18 18 6*0 1 3 7 e 1c 38 70 e0 c0 80 6*0 3e 63 63 63 6b 6b 63 63 63 3e 6*0 c 1c
  //   3c 6*c 3f 6*0 3e 63 3 6 c 18 30 61 63 7f 6*0 3e 63 3 3 1e 3 3 3 63 3e 6*0 6 e 1e 36 66 66 7f 6 6 f
  //   6*0 7f 60 60 60 7e 3 3 63 73 3e 6*0 1c 30 60 60 7e 4*63 3e 6*0 7f 63 3 6 6 c c 18 18 18 6*0 3e 63 63
  //   63 3e 4*63 3e 6*0 3e 4*63 3f 3 3 6 3c 9*0 18 18 0 0 0 18 18 9*0 18 18 0 0 0 18 18 18 30 5*0 6 c 18
  //   30 60 30 18 c 6 10*0 7e 0 0 7e 9*0 60 30 18 c 6 c 18 30 60 6*0 3e 63 63 6 c c c 0 c c 6*0 3e 63 63
  //   6f 6b 6b 6e 60 60 3e 6*0 8 1c 36 63 63 63 7f 63 63 63 6*0 7e 33 33 33 3e 4*33 7e 6*0 1e 33 61 4*60
  //   61 33 1e 6*0 7c 36 6*33 36 7c 6*0 7f 33 31 34 3c 34 30 31 33 7f 6*0 7f 33 31 34 3c 34 30 30 30 78
  //   6*0 1e 33 61 60 60 6f 63 63 37 1d 6*0 4*63 7f 5*63 6*0 3c 8*18 3c 6*0 f 6*6 66 66 3c 6*0 73 33 36 36
  //   3c 36 36 33 33 73 6*0 78 6*30 31 33 7f 6*0 63 77 7f 6b 6*63 6*0 63 63 73 7b 7f 6f 67 63 63 63 6*0 1c
  //   36 6*63 36 1c 6*0 7e 33 33 33 3e 4*30 78 6*0 3e 6*63 6b 6f 3e 6 7 4*0 7e 33 33 33 3e 36 36 33 33 73
  //   6*0 3e 63 63 30 1c 6 3 63 63 3e 6*0 ff db 99 6*18 3c 6*0 9*63 3e 6*0 7*63 36 1c 8 6*0 5*63 6b 6b 7f
  //   36 36 6*0 c3 c3 66 3c 18 18 3c 66 c3 c3 6*0 c3 c3 c3 66 3c 4*18 3c 6*0 7f 63 43 6 c 18 30 61 63 7f
  //   6*0 3c 8*30 3c 6*0 80 c0 e0 70 38 1c e 7 3 1 6*0 3c 8*c 3c 4*0 8 1c 36 63 24*0 ff 0 0 0 18 18 c 18*0
  //   3c 46 6 3e 66 66 3b 6*0 70 30 30 3c 36 4*33 6e 9*0 3e 63 60 60 60 63 3e 6*0 e 6 6 1e 36 4*66 3b 9*0
  //   3e 63 63 7e 60 63 3e 6*0 1c 36 32 30 7c 4*30 78 9*0 3b 4*66 3e 6 66 3c 4*0 70 30 30 36 3b 4*33 73
  //   6*0 c c 0 1c 5*c 1e 6*0 6 6 0 e 5*6 66 66 3c 4*0 70 30 30 33 33 36 3c 36 33 73 6*0 1c 8*c 1e 9*0 6e
  //   7f 5*6b 9*0 6e 6*33 9*0 3e 5*63 3e 9*0 6e 4*33 3e 30 30 78 7*0 3b 4*66 3e 6 6 f 7*0 6e 3b 33 30 30
  //   30 78 9*0 3e 63 38 e 3 63 3e 6*0 8 18 18 7e 4*18 1b e 9*0 6*66 3b 9*0 63 63 36 36 1c 1c 8 9*0 63 63
  //   63 6b 6b 7f 36 9*0 63 36 1c 1c 1c 36 63 9*0 5*63 3f 3 6 3c 7*0 7f 66 c 18 30 63 7f 6*0 e 18 18 18 70
  //   4*18 e 6*0 5*18 0 5*18 5*0 70 18 18 18 e 4*18 70 6*0 3b 6e 13*0 70 d8 d8 70
  //   contents of rom_6 (hex, n*v repeats v):
  //   18*0 18 3c 3c 3c 18 18 18 0 18 18 5*0 63 63 63 22 14*0 36 36 7f 36 36 36 7f 36 36 4*0 c c 3e 63 61
  //   60 3e 3 3 43 63 3e c c 7*0 61 63 6 c 18 33 63 7*0 1c 36 36 1c 3b 6e 66 66 3b 5*0 30 30 30 60 13*0 c
  //   18 18 4*30 18 18 c 6*0 18 c c 4*6 c c 18 8*0 42 66 3c ff 3c 66 42 9*0 18 18 18 ff 18 18 18 15*0 18
  //   18 18 30 9*0 ff 18*0 18 18 6*0 1 3 7 e 1c 38 70 e0 c0 80 6*0 3e 63 63 63 6b 6b 63 63 63 3e 6*0 c 1c
  //   3c 6*c 3f 6*0 3e 63 3 6 c 18 30 61 63 7f 6*0 3e 63 3 3 1e 3 3 3 63 3e 6*0 6 e 1e 36 66 66 7f 6 6 f
  //   6*0 7f 60 60 60 7e 3 3 63 73 3e 6*0 1c 30 60 60 7e 4*63 3e 6*0 7f 63 3 6 6 c c 18 18 18 6*0 3e 63 63
  //   63 3e 4*63 3e 6*0 3e 4*63 3f 3 3 6 3c 9*0 18 18 0 0 0 18 18 9*0 18 18 0 0 0 18 18 18 30 5*0 6 c 18
  //   30 60 30 18 c 6 10*0 7e 0 0 7e 9*0 60 30 18 c 6 c 18 30 60 6*0 3e 63 63 6 c c c 0 c c 6*0 3e 63 63
  //   6f 6b 6b 6e 60 60 3e 6*0 8 1c 36 63 63 63 7f 63 63 63 6*0 7e 33 33 33 3e 4*33 7e 6*0 1e 33 61 4*60
  //   61 33 1e 6*0 7c 36 6*33 36 7c 6*0 7f 33 31 34 3c 34 30 31 33 7f 6*0 7f 33 31 34 3c 34 30 30 30 78
  //   6*0 1e 33 61 60 60 6f 63 63 37 1d 6*0 4*63 7f 5*63 6*0 3c 8*18 3c 6*0 f 6*6 66 66 3c 6*0 73 33 36 36
  //   3c 36 36 33 33 73 6*0 78 6*30 31 33 7f 6*0 63 77 7f 6b 6*63 6*0 63 63 73 7b 7f 6f 67 63 63 63 6*0 1c
  //   36 6*63 36 1c 6*0 7e 33 33 33 3e 4*30 78 6*0 3e 6*63 6b 6f 3e 6 7 4*0 7e 33 33 33 3e 36 36 33 33 73
  //   6*0 3e 63 63 30 1c 6 3 63 63 3e 6*0 ff db 99 6*18 3c 6*0 9*63 3e 6*0 7*63 36 1c 8 6*0 5*63 6b 6b 7f
  //   36 36 6*0 c3 c3 66 3c 18 18 3c 66 c3 c3 6*0 c3 c3 c3 66 3c 4*18 3c 6*0 7f 63 43 6 c 18 30 61 63 7f
  //   6*0 3c 8*30 3c 6*0 80 c0 e0 70 38 1c e 7 3 1 6*0 3c 8*c 3c 4*0 8 1c 36 63 24*0 ff 0 0 0 18 18 c 18*0
  //   3c 46 6 3e 66 66 3b 6*0 70 30 30 3c 36 4*33 6e 9*0 3e 63 60 60 60 63 3e 6*0 e 6 6 1e 36 4*66 3b 9*0
  //   3e 63 63 7e 60 63 3e 6*0 1c 36 32 30 7c 4*30 78 9*0 3b 4*66 3e 6 66 3c 4*0 70 30 30 36 3b 4*33 73
  //   6*0 c c 0 1c 5*c 1e 6*0 6 6 0 e 5*6 66 66 3c 4*0 70 30 30 33 33 36 3c 36 33 73 6*0 1c 8*c 1e 9*0 6e
  //   7f 5*6b 9*0 6e 6*33 9*0 3e 5*63 3e 9*0 6e 4*33 3e 30 30 78 7*0 3b 4*66 3e 6 6 f 7*0 6e 3b 33 30 30
  //   30 78 9*0 3e 63 38 e 3 63 3e 6*0 8 18 18 7e 4*18 1b e 9*0 6*66 3b 9*0 63 63 36 36 1c 1c 8 9*0 63 63
  //   63 6b 6b 7f 36 9*0 63 36 1c 1c 1c 36 63 9*0 5*63 3f 3 6 3c 7*0 7f 66 c 18 30 63 7f 6*0 e 18 18 18 70
  //   4*18 e 6*0 5*18 0 5*18 5*0 70 18 18 18 e 4*18 70 6*0 3b 6e 13*0 70 d8 d8 70
  //   contents of rom_7 (hex, n*v repeats v):
  //   18*0 18 3c 3c 3c 18 18 18 0 18 18 5*0 63 63 63 22 14*0 36 36 7f 36 36 36 7f 36 36 4*0 c c 3e 63 61
  //   60 3e 3 3 43 63 3e c c 7*0 61 63 6 c 18 33 63 7*0 1c 36 36 1c 3b 6e 66 66 3b 5*0 30 30 30 60 13*0 c
  //   18 18 4*30 18 18 c 6*0 18 c c 4*6 c c 18 8*0 42 66 3c ff 3c 66 42 9*0 18 18 18 ff 18 18 18 15*0 18
  //   18 18 30 9*0 ff 18*0 18 18 6*0 1 3 7 e 1c 38 70 e0 c0 80 6*0 3e 63 63 63 6b 6b 63 63 63 3e 6*0 c 1c
  //   3c 6*c 3f 6*0 3e 63 3 6 c 18 30 61 63 7f 6*0 3e 63 3 3 1e 3 3 3 63 3e 6*0 6 e 1e 36 66 66 7f 6 6 f
  //   6*0 7f 60 60 60 7e 3 3 63 73 3e 6*0 1c 30 60 60 7e 4*63 3e 6*0 7f 63 3 6 6 c c 18 18 18 6*0 3e 63 63
  //   63 3e 4*63 3e 6*0 3e 4*63 3f 3 3 6 3c 9*0 18 18 0 0 0 18 18 9*0 18 18 0 0 0 18 18 18 30 5*0 6 c 18
  //   30 60 30 18 c 6 10*0 7e 0 0 7e 9*0 60 30 18 c 6 c 18 30 60 6*0 3e 63 63 6 c c c 0 c c 6*0 3e 63 63
  //   6f 6b 6b 6e 60 60 3e 6*0 8 1c 36 63 63 63 7f 63 63 63 6*0 7e 33 33 33 3e 4*33 7e 6*0 1e 33 61 4*60
  //   61 33 1e 6*0 7c 36 6*33 36 7c 6*0 7f 33 31 34 3c 34 30 31 33 7f 6*0 7f 33 31 34 3c 34 30 30 30 78
  //   6*0 1e 33 61 60 60 6f 63 63 37 1d 6*0 4*63 7f 5*63 6*0 3c 8*18 3c 6*0 f 6*6 66 66 3c 6*0 73 33 36 36
  //   3c 36 36 33 33 73 6*0 78 6*30 31 33 7f 6*0 63 77 7f 6b 6*63 6*0 63 63 73 7b 7f 6f 67 63 63 63 6*0 1c
  //   36 6*63 36 1c 6*0 7e 33 33 33 3e 4*30 78 6*0 3e 6*63 6b 6f 3e 6 7 4*0 7e 33 33 33 3e 36 36 33 33 73
  //   6*0 3e 63 63 30 1c 6 3 63 63 3e 6*0 ff db 99 6*18 3c 6*0 9*63 3e 6*0 7*63 36 1c 8 6*0 5*63 6b 6b 7f
  //   36 36 6*0 c3 c3 66 3c 18 18 3c 66 c3 c3 6*0 c3 c3 c3 66 3c 4*18 3c 6*0 7f 63 43 6 c 18 30 61 63 7f
  //   6*0 3c 8*30 3c 6*0 80 c0 e0 70 38 1c e 7 3 1 6*0 3c 8*c 3c 4*0 8 1c 36 63 24*0 ff 0 0 0 18 18 c 18*0
  //   3c 46 6 3e 66 66 3b 6*0 70 30 30 3c 36 4*33 6e 9*0 3e 63 60 60 60 63 3e 6*0 e 6 6 1e 36 4*66 3b 9*0
  //   3e 63 63 7e 60 63 3e 6*0 1c 36 32 30 7c 4*30 78 9*0 3b 4*66 3e 6 66 3c 4*0 70 30 30 36 3b 4*33 73
  //   6*0 c c 0 1c 5*c 1e 6*0 6 6 0 e 5*6 66 66 3c 4*0 70 30 30 33 33 36 3c 36 33 73 6*0 1c 8*c 1e 9*0 6e
  //   7f 5*6b 9*0 6e 6*33 9*0 3e 5*63 3e 9*0 6e 4*33 3e 30 30 78 7*0 3b 4*66 3e 6 6 f 7*0 6e 3b 33 30 30
  //   30 78 9*0 3e 63 38 e 3 63 3e 6*0 8 18 18 7e 4*18 1b e 9*0 6*66 3b 9*0 63 63 36 36 1c 1c 8 9*0 63 63
  //   63 6b 6b 7f 36 9*0 63 36 1c 1c 1c 36 63 9*0 5*63 3f 3 6 3c 7*0 7f 66 c 18 30 63 7f 6*0 e 18 18 18 70
  //   4*18 e 6*0 5*18 0 5*18 5*0 70 18 18 18 e 4*18 70 6*0 3b 6e 13*0 70 d8 d8 70
  //   contents of rom_8 (hex, n*v repeats v):
  //   18*0 18 3c 3c 3c 18 18 18 0 18 18 5*0 63 63 63 22 14*0 36 36 7f 36 36 36 7f 36 36 4*0 c c 3e 63 61
  //   60 3e 3 3 43 63 3e c c 7*0 61 63 6 c 18 33 63 7*0 1c 36 36 1c 3b 6e 66 66 3b 5*0 30 30 30 60 13*0 c
  //   18 18 4*30 18 18 c 6*0 18 c c 4*6 c c 18 8*0 42 66 3c ff 3c 66 42 9*0 18 18 18 ff 18 18 18 15*0 18
  //   18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
  //   提示：使用只读存储器ROM加载ASCII码点阵字库、ROM片选信号高电平有效
  //   输出引脚
  //   contents of rom_9 (hex, n*v repeats v):
  //   18*0 18 3c 3c 3c 18 18 18 0 18 18 5*0 63 63 63 22 14*0 36 36 7f 36 36 36 7f 36 36 4*0 c c 3e 63 61
  //   60 3e 3 3 43 63 3e c c 7*0 61 63 6 c 18 33 63 7*0 1c 36 36 1c 3b 6e 66 66 3b 5*0 30 30 30 60 13*0 c
  //   18 18 4*30 18 18 c 6*0 18 c c 4*6 c c 18 8*0 42 66 3c ff 3c 66 42 9*0 18 18 18 ff 18 18 18 15*0 18
  //   18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
  //   contents of rom_10 (hex, n*v repeats v):
  //   18*0 18 3c 3c 3c 18 18 18 0 18 18 5*0 63 63 63 22 14*0 36 36 7f 36 36 36 7f 36 36 4*0 c c 3e 63 61
  //   60 3e 3 3 43 63 3e c c 7*0 61 63 6 c 18 33 63 7*0 1c 36 36 1c 3b 6e 66 66 3b 5*0 30 30 30 60 13*0 c
  //   18 18 4*30 18 18 c 6*0 18 c c 4*6 c c 18 8*0 42 66 3c ff 3c 66 42 9*0 18 18 18 ff 18 18 18 15*0 18
  //   18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
  //   contents of rom_11 (hex, n*v repeats v):
  //   18*0 18 3c 3c 3c 18 18 18 0 18 18 5*0 63 63 63 22 14*0 36 36 7f 36 36 36 7f 36 36 4*0 c c 3e 63 61
  //   60 3e 3 3 43 63 3e c c 7*0 61 63 6 c 18 33 63 7*0 1c 36 36 1c 3b 6e 66 66 3b 5*0 30 30 30 60 13*0 c
  //   18 18 4*30 18 18 c 6*0 18 c c 4*6 c c 18 8*0 42 66 3c ff 3c 66 42 9*0 18 18 18 ff 18 18 18 15*0 18
  //   18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
  //   contents of rom_12 (hex, n*v repeats v):
  //   18*0 18 3c 3c 3c 18 18 18 0 18 18 5*0 63 63 63 22 14*0 36 36 7f 36 36 36 7f 36 36 4*0 c c 3e 63 61
  //   60 3e 3 3 43 63 3e c c 7*0 61 63 6 c 18 33 63 7*0 1c 36 36 1c 3b 6e 66 66 3b 5*0 30 30 30 60 13*0 c
  //   18 18 4*30 18 18 c 6*0 18 c c 4*6 c c 18 8*0 42 66 3c ff 3c 66 42 9*0 18 18 18 ff 18 18 18 15*0 18
  //   18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
  //   contents of rom_13 (hex, n*v repeats v):
  //   18*0 18 3c 3c 3c 18 18 18 0 18 18 5*0 63 63 63 22 14*0 36 36 7f 36 36 36 7f 36 36 4*0 c c 3e 63 61
  //   60 3e 3 3 43 63 3e c c 7*0 61 63 6 c 18 33 63 7*0 1c 36 36 1c 3b 6e 66 66 3b 5*0 30 30 30 60 13*0 c
  //   18 18 4*30 18 18 c 6*0 18 c c 4*6 c c 18 8*0 42 66 3c ff 3c 66 42 9*0 18 18 18 ff 18 18 18 15*0 18
  //   18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
  //   contents of rom_14 (hex, n*v repeats v):
  //   18*0 18 3c 3c 3c 18 18 18 0 18 18 5*0 63 63 63 22 14*0 36 36 7f 36 36 36 7f 36 36 4*0 c c 3e 63 61
  //   60 3e 3 3 43 63 3e c c 7*0 61 63 6 c 18 33 63 7*0 1c 36 36 1c 3b 6e 66 66 3b 5*0 30 30 30 60 13*0 c
  //   18 18 4*30 18 18 c 6*0 18 c c 4*6 c c 18 8*0 42 66 3c ff 3c 66 42 9*0 18 18 18 ff 18 18 18 15*0 18
  //   18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
  //   contents of rom_15 (hex, n*v repeats v):
  //   18*0 18 3c 3c 3c 18 18 18 0 18 18 5*0 63 63 63 22 14*0 36 36 7f 36 36 36 7f 36 36 4*0 c c 3e 63 61
  //   60 3e 3 3 43 63 3e c c 7*0 61 63 6 c 18 33 63 7*0 1c 36 36 1c 3b 6e 66 66 3b 5*0 30 30 30 60 13*0 c
  //   18 18 4*30 18 18 c 6*0 18 c c 4*6 c c 18 8*0 42 66 3c ff 3c 66 42 9*0 18 18 18 ff 18 18 18 15*0 18
  //   18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
  //   contents of rom_16 (hex, n*v repeats v):
  //   18*0 18 3c 3c 3c 18 18 18 0 18 18 5*0 63 63 63 22 14*0 36 36 7f 36 36 36 7f 36 36 4*0 c c 3e 63 61
  //   60 3e 3 3 43 63 3e c c 7*0 61 63 6 c 18 33 63 7*0 1c 36 36 1c 3b 6e 66 66 3b 5*0 30 30 30 60 13*0 c
  //   18 18 4*30 18 18 c 6*0 18 c c 4*6 c c 18 8*0 42 66 3c ff 3c 66 42 9*0 18 18 18 ff 18 18 18 15*0 18
  //   18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
endmodule
