// Logisim project lab5.2.circ as structural Verilog: 1 circuit, main circuit DataRam
// DataRAM
module DataRam (
  input  CLK,
  input  CLR,
  input  WE,
  input  [2:0] MemOp,
  input  [17:0] Addr,
  input  [31:0] Din,
  output AlignErr,
  output [31:0] DataOut
);

  wire and_1_out, and_2_out, and_3_out, and_4_out, and_5_out, and_6_out, and_7_out, and_8_out, and_9_out,
       and_10_out, and_11_out, and_12_out, and_13_out, and_14_out, and_15_out, and_16_out, and_17_out,
       and_18_out, and_19_out, and_20_out;
  wire [3:0] or_5_out;
  wire [7:0] multiplexer_1_out, multiplexer_2_out, multiplexer_3_out, multiplexer_4_out, multiplexer_5_out,
       ram_1_data, ram_2_data, ram_3_data, ram_4_data;
  wire [15:0] multiplexer_6_out;
  wire [31:0] bit_extender_1_out, bit_extender_2_out, bit_extender_3_out, bit_extender_4_out;

  // Probe on Addr
  and and_1 (and_1_out, ~MemOp[0], ~MemOp[1], ~MemOp[2], ~Addr[0], ~Addr[1]);  // AND_Gate
  and and_2 (and_2_out, MemOp[0], ~MemOp[1], Addr[0], Addr[1]);  // AND_Gate
  and and_3 (and_3_out, ~MemOp[0], MemOp[1], ~Addr[0], Addr[1]);  // AND_Gate
  // Probe on Din
  Multiplexer #(.select(4), .width(8), .enable("false")) multiplexer_1 (
    .in8(Din[7:0]), .in12(Din[15:8]), .in15(Din[31:24]), .out(multiplexer_1_out), .sel(or_5_out));  // open: in0, in1, in2, in3, in4, in5, in6, in7, in9, in10, in11, in13, in14
  or or_1 (or_5_out[3], and_1_out, and_2_out, and_3_out);
  Multiplexer #(.select(4), .width(8), .enable("false")) multiplexer_2 (
    .in4(Din[7:0]), .in12(Din[7:0]), .in15(Din[23:16]), .out(multiplexer_2_out), .sel(or_5_out));  // open: in0, in1, in2, in3, in5, in6, in7, in8, in9, in10, in11, in13, in14
  RAM #(.addrWidth(16), .bus("separate"), .Select("high"), .simpleMode("false")) ram_1 (
    .addr(Addr[17:2]), .din(multiplexer_1_out), .data(ram_1_data), .str(WE), .sel(or_5_out[3]), .clk(CLK),
    .clr(CLR));  // open: ld
  and and_4 (and_4_out, ~MemOp[0], ~MemOp[1], ~MemOp[2], ~Addr[0], ~Addr[1]);  // AND_Gate
  and and_5 (and_5_out, MemOp[0], ~MemOp[1], ~Addr[0], Addr[1]);  // AND_Gate
  and and_6 (and_6_out, ~MemOp[0], MemOp[1], ~Addr[0], Addr[1]);  // AND_Gate
  and and_7 (and_7_out, Addr[0], ~Addr[1], ~MemOp[1], ~MemOp[0]);  // AND_Gate
  and and_8 (and_8_out, Addr[1], ~Addr[0], ~MemOp[0], ~MemOp[1]);  // AND_Gate
  and and_9 (and_9_out, Addr[1], Addr[0], ~MemOp[0], ~MemOp[1]);  // AND_Gate
  and and_10 (and_10_out, MemOp[2], ~MemOp[1], ~MemOp[0], ~Addr[0], ~Addr[1]);  // AND_Gate
  // Probe on MemOp
  or or_2 (or_5_out[2], and_4_out, and_5_out, and_6_out);
  // Probe on DataOut
  Multiplexer #(.select(4), .width(8), .enable("false")) multiplexer_3 (
    .in2(Din[7:0]), .in3(Din[15:8]), .in15(Din[15:8]), .out(multiplexer_3_out), .sel(or_5_out));  // open: in0, in1, in4, in5, in6, in7, in8, in9, in10, in11, in12, in13, in14
  RAM #(.addrWidth(16), .bus("separate"), .Select("high"), .simpleMode("false")) ram_2 (
    .addr(Addr[17:2]), .din(multiplexer_2_out), .data(ram_2_data), .str(WE), .sel(or_5_out[2]), .clk(CLK),
    .clr(CLR));  // open: ld
  and and_11 (and_11_out, ~MemOp[0], ~MemOp[1], ~MemOp[2], ~Addr[0], ~Addr[1]);  // AND_Gate
  and and_12 (and_12_out, MemOp[0], ~MemOp[1], Addr[0], ~Addr[1]);  // AND_Gate
  and and_13 (and_13_out, ~MemOp[0], MemOp[1], ~Addr[0], ~Addr[1]);  // AND_Gate
  and and_14 (and_14_out, Addr[0], ~Addr[1], MemOp[1], ~MemOp[0]);  // AND_Gate
  and and_15 (and_15_out, MemOp[1], ~MemOp[0], Addr[0], Addr[1]);  // AND_Gate
  and and_16 (and_16_out, MemOp[1], MemOp[0]);
  or or_3 (or_5_out[1], and_11_out, and_12_out, and_13_out);
  Multiplexer #(.select(4), .width(8), .enable("false")) multiplexer_4 (
    .in1(Din[7:0]), .in3(Din[7:0]), .in15(Din[7:0]), .out(multiplexer_4_out), .sel(or_5_out));  // open: in0, in2, in4, in5, in6, in7, in8, in9, in10, in11, in12, in13, in14
  RAM #(.addrWidth(16), .bus("separate"), .Select("high"), .simpleMode("false")) ram_3 (
    .addr(Addr[17:2]), .din(multiplexer_3_out), .data(ram_3_data), .str(WE), .sel(or_5_out[1]), .clk(CLK),
    .clr(CLR));  // open: ld
  and and_17 (and_17_out, ~MemOp[0], ~MemOp[1], ~MemOp[2], ~Addr[0], ~Addr[1]);  // AND_Gate
  and and_18 (and_18_out, MemOp[0], ~MemOp[1], ~Addr[0], ~Addr[1]);  // AND_Gate
  and and_19 (and_19_out, ~MemOp[0], MemOp[1], ~Addr[0], ~Addr[1]);  // AND_Gate
  or or_4 (AlignErr, and_7_out, and_8_out, and_9_out, and_10_out, and_14_out, and_15_out, and_16_out);
  RAM #(.addrWidth(16), .bus("separate"), .Select("high"), .simpleMode("false")) ram_4 (
    .addr(Addr[17:2]), .din(multiplexer_4_out), .data(ram_4_data), .str(WE), .sel(or_5_out[0]), .clk(CLK),
    .clr(CLR));  // open: ld
  or or_5 (or_5_out[0], and_17_out, and_18_out, and_19_out);
  Multiplexer #(.select(2), .width(8), .enable("false")) multiplexer_5 (
    .in0(ram_4_data), .in1(ram_3_data), .in2(ram_2_data), .in3(ram_1_data), .out(multiplexer_5_out),
    .sel(Addr[1:0]));
  and and_20 (and_20_out, ~Addr[0], Addr[1]);  // AND_Gate
  assign bit_extender_1_out = {{24{multiplexer_5_out[7]}}, multiplexer_5_out};  // Bit_Extender bit_extender_1
  assign bit_extender_2_out = {{24{1'b0}}, multiplexer_5_out};  // Bit_Extender bit_extender_2
  assign bit_extender_3_out = {{16{1'b0}}, multiplexer_6_out};  // Bit_Extender bit_extender_3
  assign bit_extender_4_out = {{16{multiplexer_6_out[15]}}, multiplexer_6_out};  // Bit_Extender bit_extender_4
  Multiplexer #(.width(16), .enable("false")) multiplexer_6 (
    .in0({ram_3_data, ram_4_data}), .in1({ram_1_data, ram_2_data}), .out(multiplexer_6_out), .sel(and_20_out));
  Multiplexer #(.select(3), .width(32), .enable("false")) multiplexer_7 (
    .in0({ram_1_data, ram_2_data, ram_3_data, ram_4_data}), .in1(bit_extender_2_out),
    .in2(bit_extender_3_out), .in5(bit_extender_1_out), .in6(bit_extender_4_out), .out(DataOut), .sel(MemOp));  // open: in3, in4, in7

  // Other names for the same wires on the sheet: Dout[31:0] = DataOut

  // Notes on the sheet:
  //   输入引脚
  //   请勿修改引脚名称、电路名称及电路封装外观
  //   为了后续实验中的引用，不要修改MemOp的编码定义、引脚名称和在布局中的位置。
  //   32位数据存储器，按字节分4片存储，可按照字节、半字和字进行存储；读取字节或半字时，支持0扩展和符号位扩展。
  //   输出引脚
endmodule
