// Logisim project lab5.5.circ as structural Verilog: 3 circuits, main circuit main
module main (
  input  [2:0] ExtOp,
  input  [2:0] MemOp,
  input  RegWr,
  input  ALUASrc,
  input  MemWr,
  input  [1:0] ALUBSrc,
  input  [31:0] Initial_Address,
  input  [3:0] ALUctr,
  input  MemToReg,
  input  [2:0] Branch,
  input  clk,
  input  ReSet,
  output [31:0] PC,
  output [31:0] BusW,
  output [31:0] Din,
  output NxtASrc,
  output NxtBSrc
);

  wire alu_1_zero;
  wire [31:0] alu_1_s, dataram_1_dataout, idu_1_busa, idu_1_busb, idu_1_dataa, idu_1_datab, idu_1_imm,
       \指令存储器_data ;

  // Probe on Initial_Address
  IFU ifu_1 (
    .CLK(clk), .Reset(ReSet), .NxtASrc(NxtASrc), .NxtBSrc(NxtBSrc), .Initial_Address(Initial_Address),
    .Imm(idu_1_imm), .BusA(idu_1_busa), .PC(PC));
  ROM #(.addrWidth(16), .dataWidth(32), .Select("high")) \u_指令存储器  (.addr(PC[17:2]), .data(\指令存储器_data ));
  // Probe on PC
  IDU idu_1 (
    .ExtOp(ExtOp), .RegWr(RegWr), .ALUASrc(ALUASrc), .ALUBSrc(ALUBSrc), .IR(\指令存储器_data ), .BusW(BusW),
    .PC(PC), .DataA(idu_1_dataa), .BusB(idu_1_busb), .DataB(idu_1_datab), .Imm(idu_1_imm), .BusA(idu_1_busa),
    .CLK(clk));  // open: OpCode, Funct3, Funct7
  Multiplexer #(.width(32), .enable("false")) multiplexer_1 (.in0(idu_1_busb), .out(Din), .sel(ReSet));  // open: in1
  // Probe on BusW
  ALU alu_1 (.A(idu_1_dataa), .B(idu_1_datab), .S(alu_1_s), .ALUctr(ALUctr), .Zero(alu_1_zero));
  // Probe on Din
  Branch branch_1 (.Branch(Branch), .NxtASrc(NxtASrc), .Zero(alu_1_zero), .NxtBSrc(NxtBSrc), .Result0(alu_1_s[0]));
  DataRam dataram_1 (
    .Addr(alu_1_s[17:0]), .Din(idu_1_busb), .DataOut(dataram_1_dataout), .CLK(clk), .CLR(ReSet),
    .MemOp(MemOp), .WE(MemWr));  // open: AlignErr
  Multiplexer #(.width(32), .enable("false")) multiplexer_2 (
    .in0(alu_1_s), .in1(dataram_1_dataout), .out(BusW), .sel(MemToReg));

  // Other names for the same wires on the sheet: Init_Addr[31:0] = Initial_Address

  // Notes on the sheet:
  //   ALUctr: pull=down
  //   ALUASrc: pull=down
  //   Branch: pull=down
  //   ExtOp: pull=down
  //   NxtBSrc: pull=down
  //   ALUBSrc: pull=down
  //   RegWr: pull=down
  //   NxtASrc: pull=down
  //   输入信号
  //   contents of 指令存储器 (hex, n*v repeats v):
  //   8000ef ffdff06f 100013 deadc2b7 eef28293 52d333 135313 4052d3b3 529e33 1e1e13 6e0eb3 1000513 5500a3
  //   551223 551323 552423 150483 154903 451983 655a03 452a83 a55b03 ffff0bb7 17afc33 16c6cb3 fb9e92e3 73
  //   请勿修改引脚名称、电路名称及电路封装外观
  //   为了后续实验中的引用，不要修改控制信号的编码定义、引脚名称和在布局中的位置。
  //   指令存储器和数据存储器数据位都是32位，指令存储器编址以字为单位，数据存储器编址以字节为单位。
  //   32位数据存储器，按字节分4片存储，可按照字节、半字和字进行存储；读取字节或半字时，支持0扩展和符号位扩展。
  //   输出信号
endmodule

module Branch (
  input  [2:0] Branch,
  input  Zero,
  input  Result0,
  output NxtASrc,
  output NxtBSrc
);

  wire not_1_out, or_1_out;

  or or_1 (or_1_out, ~Result0, Zero);  // OR_Gate
  not not_1 (not_1_out, Zero);
  Multiplexer #(.select(3), .enable("false")) multiplexer_1 (
    .in0(1'b0), .in1(1'b1), .in2(1'b1), .in4(Zero), .in5(not_1_out), .in6(Result0), .in7(or_1_out),
    .out(NxtBSrc), .sel(Branch));  // open: in3
  Multiplexer #(.select(3), .enable("false")) multiplexer_2 (
    .in0(1'b0), .in1(1'b0), .in2(1'b1), .in4(1'b0), .in5(1'b0), .in6(1'b0), .in7(1'b0), .out(NxtASrc),
    .sel(Branch));  // open: in3

  // Notes on the sheet:
  //   Branch: pull=down
  //   Zero: pull=down
  //   输入信号
  //   请勿修改引脚名称、电路名称及电路封装外观
  //   不要修改控制信号的编码定义、引脚名称和在布局中的位置。
  //   输出信号
endmodule

module IFU (
  input  [31:0] Initial_Address,
  input  [31:0] Imm,
  input  [31:0] BusA,
  input  CLK,
  input  Reset,
  input  NxtASrc,
  input  NxtBSrc,
  output [31:0] PC
);

  wire [31:0] adder_1_out, multiplexer_1_out, multiplexer_2_out, multiplexer_3_out;

  Multiplexer #(.width(32), .enable("false")) multiplexer_1 (
    .in0(PC), .in1(BusA), .out(multiplexer_1_out), .sel(NxtASrc));
  Multiplexer #(.width(32), .enable("false")) multiplexer_2 (
    .in0(32'h4), .in1(Imm), .out(multiplexer_2_out), .sel(NxtBSrc));
  Adder #(.width(32)) adder_1 (.a(multiplexer_1_out), .b(multiplexer_2_out), .out(adder_1_out));  // open: cin, cout
  Multiplexer #(.width(32), .enable("false")) multiplexer_3 (
    .in0(adder_1_out), .in1(Initial_Address), .out(multiplexer_3_out), .sel(Reset));
  Register #(.width(32), .Select("low")) u_PC (.D(multiplexer_3_out), .Q(PC), .clk(CLK));  // open: en, clr

  // Other names for the same wires on the sheet: Init_Addr[31:0] = Initial_Address

  // Notes on the sheet:
  //   BusA: pull=down
  //   Imm: pull=down
  //   NxtASrc: pull=down
  //   NxtBSrc: pull=down
  //   输入信号
  //   请勿修改引脚名称、电路名称及电路封装外观
  //   指令存储器256KB，数据位为32位，地址位为16位。PC寄存器数据宽度32位，片选信号高电平有效
  //   输出信号
endmodule
