// Logisim project lab5.思考题1.circ as structural Verilog: 2 circuits, main circuit main
module main (
  input  in_1
);

  wire clock_1_out;
  wire [7:0] adder_1_out, adder_2_out, counter_1_q, \寄存器_1_out_3 , \寄存器_1_out_4 , \寄存器_1_out_5 ,
       \寄存器_1_out_6 , \寄存器_1_out_7 , \寄存器_1_out_8 , \寄存器_1_out_9 , \寄存器_1_out_10 , \寄存器_1_out_11 ,
       \寄存器_1_out_12 , \寄存器_1_out_13 , \寄存器_1_out_14 , \寄存器_1_out_15 , \寄存器_1_out_16 , \寄存器_1_out_17 ,
       \寄存器_1_out_18 , \寄存器_2_out_3 , \寄存器_2_out_4 , \寄存器_2_out_5 , \寄存器_2_out_6 , \寄存器_2_out_7 ,
       \寄存器_2_out_8 , \寄存器_2_out_9 , \寄存器_2_out_10 , \寄存器_2_out_11 , \寄存器_2_out_12 , \寄存器_2_out_13 ,
       \寄存器_2_out_14 , \寄存器_2_out_15 , \寄存器_2_out_16 , \寄存器_2_out_17 , \寄存器_2_out_18 , \寄存器_3_out_3 ,
       \寄存器_3_out_4 , \寄存器_3_out_5 , \寄存器_3_out_6 , \寄存器_3_out_7 , \寄存器_3_out_8 , \寄存器_3_out_9 ,
       \寄存器_3_out_10 , \寄存器_3_out_11 , \寄存器_3_out_12 , \寄存器_3_out_13 , \寄存器_3_out_14 , \寄存器_3_out_15 ,
       \寄存器_3_out_16 , \寄存器_3_out_17 , \寄存器_3_out_18 ;

  Counter #(.max('h50)) counter_1 (
    .Q(counter_1_q), .clk(clock_1_out));  // open: load, D, count, carry, clr, preset, down
  Clock clock_1 (.out(clock_1_out));
  Adder adder_1 (.a(counter_1_q), .b(8'h10), .out(adder_1_out));  // open: cin, cout
  Adder adder_2 (.a(adder_1_out), .b(8'h10), .out(adder_2_out));  // open: cin, cout
  DotMatrix #(.inputtype("row"), .matrixcols(8), .matrixrows(16)) dotmatrix_1 (
    .row0(\寄存器_1_out_3 ), .row1(\寄存器_1_out_4 ), .row2(\寄存器_1_out_5 ), .row3(\寄存器_1_out_6 ),
    .row4(\寄存器_1_out_7 ), .row5(\寄存器_1_out_8 ), .row6(\寄存器_1_out_9 ), .row7(\寄存器_1_out_10 ),
    .row8(\寄存器_1_out_11 ), .row9(\寄存器_1_out_12 ), .row10(\寄存器_1_out_13 ), .row11(\寄存器_1_out_14 ),
    .row12(\寄存器_1_out_15 ), .row13(\寄存器_1_out_16 ), .row14(\寄存器_1_out_17 ), .row15(\寄存器_1_out_18 ));
  \寄存器  \u_寄存器_1  (
    .ASCII_CODE(counter_1_q), .Sel(in_1), .out_3(\寄存器_1_out_3 ), .out_4(\寄存器_1_out_4 ),
    .out_5(\寄存器_1_out_5 ), .out_6(\寄存器_1_out_6 ), .out_7(\寄存器_1_out_7 ), .out_8(\寄存器_1_out_8 ),
    .out_9(\寄存器_1_out_9 ), .out_10(\寄存器_1_out_10 ), .out_11(\寄存器_1_out_11 ), .out_12(\寄存器_1_out_12 ),
    .out_13(\寄存器_1_out_13 ), .out_14(\寄存器_1_out_14 ), .out_15(\寄存器_1_out_15 ), .out_16(\寄存器_1_out_16 ),
    .out_17(\寄存器_1_out_17 ), .out_18(\寄存器_1_out_18 ));
  DotMatrix #(.inputtype("row"), .matrixcols(8), .matrixrows(16)) dotmatrix_2 (
    .row0(\寄存器_2_out_3 ), .row1(\寄存器_2_out_4 ), .row2(\寄存器_2_out_5 ), .row3(\寄存器_2_out_6 ),
    .row4(\寄存器_2_out_7 ), .row5(\寄存器_2_out_8 ), .row6(\寄存器_2_out_9 ), .row7(\寄存器_2_out_10 ),
    .row8(\寄存器_2_out_11 ), .row9(\寄存器_2_out_12 ), .row10(\寄存器_2_out_13 ), .row11(\寄存器_2_out_14 ),
    .row12(\寄存器_2_out_15 ), .row13(\寄存器_2_out_16 ), .row14(\寄存器_2_out_17 ), .row15(\寄存器_2_out_18 ));
  \寄存器  \u_寄存器_2  (
    .ASCII_CODE(adder_1_out), .Sel(in_1), .out_3(\寄存器_2_out_3 ), .out_4(\寄存器_2_out_4 ),
    .out_5(\寄存器_2_out_5 ), .out_6(\寄存器_2_out_6 ), .out_7(\寄存器_2_out_7 ), .out_8(\寄存器_2_out_8 ),
    .out_9(\寄存器_2_out_9 ), .out_10(\寄存器_2_out_10 ), .out_11(\寄存器_2_out_11 ), .out_12(\寄存器_2_out_12 ),
    .out_13(\寄存器_2_out_13 ), .out_14(\寄存器_2_out_14 ), .out_15(\寄存器_2_out_15 ), .out_16(\寄存器_2_out_16 ),
    .out_17(\寄存器_2_out_17 ), .out_18(\寄存器_2_out_18 ));
  DotMatrix #(.inputtype("row"), .matrixcols(8), .matrixrows(16)) dotmatrix_3 (
    .row0(\寄存器_3_out_3 ), .row1(\寄存器_3_out_4 ), .row2(\寄存器_3_out_5 ), .row3(\寄存器_3_out_6 ),
    .row4(\寄存器_3_out_7 ), .row5(\寄存器_3_out_8 ), .row6(\寄存器_3_out_9 ), .row7(\寄存器_3_out_10 ),
    .row8(\寄存器_3_out_11 ), .row9(\寄存器_3_out_12 ), .row10(\寄存器_3_out_13 ), .row11(\寄存器_3_out_14 ),
    .row12(\寄存器_3_out_15 ), .row13(\寄存器_3_out_16 ), .row14(\寄存器_3_out_17 ), .row15(\寄存器_3_out_18 ));
  \寄存器  \u_寄存器_3  (
    .ASCII_CODE(adder_2_out), .Sel(in_1), .out_3(\寄存器_3_out_3 ), .out_4(\寄存器_3_out_4 ),
    .out_5(\寄存器_3_out_5 ), .out_6(\寄存器_3_out_6 ), .out_7(\寄存器_3_out_7 ), .out_8(\寄存器_3_out_8 ),
    .out_9(\寄存器_3_out_9 ), .out_10(\寄存器_3_out_10 ), .out_11(\寄存器_3_out_11 ), .out_12(\寄存器_3_out_12 ),
    .out_13(\寄存器_3_out_13 ), .out_14(\寄存器_3_out_14 ), .out_15(\寄存器_3_out_15 ), .out_16(\寄存器_3_out_16 ),
    .out_17(\寄存器_3_out_17 ), .out_18(\寄存器_3_out_18 ));
endmodule

module \寄存器  (
  input  [7:0] ASCII_CODE,
  input  Sel,
  output [7:0] out_3,
  output [7:0] out_4,
  output [7:0] out_5,
  output [7:0] out_6,
  output [7:0] out_7,
  output [7:0] out_8,
  output [7:0] out_9,
  output [7:0] out_10,
  output [7:0] out_11,
  output [7:0] out_12,
  output [7:0] out_13,
  output [7:0] out_14,
  output [7:0] out_15,
  output [7:0] out_16,
  output [7:0] out_17,
  output [7:0] out_18
);

  wire [15:0] adder_1_out, adder_2_out, adder_3_out, adder_4_out, adder_5_out, adder_6_out, adder_7_out,
       adder_8_out, adder_9_out, adder_10_out, adder_11_out, adder_12_out, adder_13_out, adder_14_out,
       adder_15_out, adder_16_out, bit_extender_1_out;

  assign bit_extender_1_out = {{8{1'b0}}, ASCII_CODE};  // Bit_Extender bit_extender_1
  Shifter #(.width(16)) shifter_1 (.\dist (4'b0100));  // open: in, out
  Adder #(.width(16)) adder_1 (.a(bit_extender_1_out), .b({16{1'b0}}), .out(adder_1_out));  // open: cin, cout
  Adder #(.width(16)) adder_2 (.a(bit_extender_1_out), .b(16'h2), .out(adder_2_out));  // open: cin, cout
  Adder #(.width(16)) adder_3 (.a(bit_extender_1_out), .b(16'h4), .out(adder_3_out));  // open: cin, cout
  Adder #(.width(16)) adder_4 (.a(bit_extender_1_out), .b(16'h6), .out(adder_4_out));  // open: cin, cout
  Adder #(.width(16)) adder_5 (.a(bit_extender_1_out), .b(16'h8), .out(adder_5_out));  // open: cin, cout
  Adder #(.width(16)) adder_6 (.a(bit_extender_1_out), .b(16'ha), .out(adder_6_out));  // open: cin, cout
  Adder #(.width(16)) adder_7 (.a(bit_extender_1_out), .b(16'hc), .out(adder_7_out));  // open: cin, cout
  Adder #(.width(16)) adder_8 (.a(bit_extender_1_out), .b(16'he), .out(adder_8_out));  // open: cin, cout
  ROM #(.addrWidth(16), .Select("high")) rom_1 (.addr(adder_1_out), .data(out_3), .sel(Sel));
  ROM #(.addrWidth(16), .Select("high")) rom_2 (.addr(adder_2_out), .data(out_5), .sel(Sel));
  ROM #(.addrWidth(16), .Select("high")) rom_3 (.addr(adder_3_out), .data(out_7), .sel(Sel));
  ROM #(.addrWidth(16), .Select("high")) rom_4 (.addr(adder_4_out), .data(out_9), .sel(Sel));
  ROM #(.addrWidth(16), .Select("high")) rom_5 (.addr(adder_5_out), .data(out_11), .sel(Sel));
  ROM #(.addrWidth(16), .Select("high")) rom_6 (.addr(adder_6_out), .data(out_13), .sel(Sel));
  ROM #(.addrWidth(16), .Select("high")) rom_7 (.addr(adder_7_out), .data(out_15), .sel(Sel));
  ROM #(.addrWidth(16), .Select("high")) rom_8 (.addr(adder_8_out), .data(out_17), .sel(Sel));
  DotMatrix #(.inputtype("row"), .matrixcols(8), .matrixrows(16)) dotmatrix_1 (
    .row0(out_3), .row1(out_4), .row2(out_5), .row3(out_6), .row4(out_7), .row5(out_8), .row6(out_9),
    .row7(out_10), .row8(out_11), .row9(out_12), .row10(out_13), .row11(out_14), .row12(out_15),
    .row13(out_16), .row14(out_17), .row15(out_18));
  Adder #(.width(16)) adder_9 (.a(bit_extender_1_out), .b(16'h1), .out(adder_9_out));  // open: cin, cout
  Adder #(.width(16)) adder_10 (.a(bit_extender_1_out), .b(16'h3), .out(adder_10_out));  // open: cin, cout
  Adder #(.width(16)) adder_11 (.a(bit_extender_1_out), .b(16'h5), .out(adder_11_out));  // open: cin, cout
  Adder #(.width(16)) adder_12 (.a(bit_extender_1_out), .b(16'h7), .out(adder_12_out));  // open: cin, cout
  Adder #(.width(16)) adder_13 (.a(bit_extender_1_out), .b(16'h9), .out(adder_13_out));  // open: cin, cout
  Adder #(.width(16)) adder_14 (.a(bit_extender_1_out), .b(16'hb), .out(adder_14_out));  // open: cin, cout
  Adder #(.width(16)) adder_15 (.a(bit_extender_1_out), .b(16'hd), .out(adder_15_out));  // open: cin, cout
  Adder #(.width(16)) adder_16 (.a(bit_extender_1_out), .b(16'hf), .out(adder_16_out));  // open: cin, cout
  ROM #(.addrWidth(16), .Select("high")) rom_9 (.addr(adder_9_out), .data(out_4), .sel(Sel));
  ROM #(.addrWidth(16), .Select("high")) rom_10 (.addr(adder_10_out), .data(out_6), .sel(Sel));
  ROM #(.addrWidth(16), .Select("high")) rom_11 (.addr(adder_11_out), .data(out_8), .sel(Sel));
  ROM #(.addrWidth(16), .Select("high")) rom_12 (.addr(adder_12_out), .data(out_10), .sel(Sel));
  ROM #(.addrWidth(16), .Select("high")) rom_13 (.addr(adder_13_out), .data(out_12), .sel(Sel));
  ROM #(.addrWidth(16), .Select("high")) rom_14 (.addr(adder_14_out), .data(out_14), .sel(Sel));
  ROM #(.addrWidth(16), .Select("high")) rom_15 (.addr(adder_15_out), .data(out_16), .sel(Sel));
  ROM #(.addrWidth(16), .Select("high")) rom_16 (.addr(adder_16_out), .data(out_18), .sel(Sel));

  // Other names for the same wires on the sheet: Code[7:0] = ASCII_CODE; row1[7:0] = out_3; row2[7:0] = out_4;
  //   row3[7:0] = out_5; row4[7:0] = out_6; row5[7:0] = out_7; row6[7:0] = out_8; row7[7:0] = out_9;
  //   row8[7:0] = out_10; row9[7:0] = out_11; row10[7:0] = out_12; row11[7:0] = out_13; row12[7:0] = out_14;
  //   row13[7:0] = out_15; row14[7:0] = out_16; row15[7:0] = out_17; row16[7:0] = out_18

  // Notes on the sheet:
  //   ASCII字库地址
  //   contents of rom_1 (hex, n*v repeats v):
  //   0 0 63 63 73 7b 7f 6f 67 63 63 63 6*0 f 6*6 66 66 3c 6*0 9*63 3e 6*0 1e 33 61 4*60 61 33 1e 6*0 3e
  //   63 63 30 1c 6 3 63 63 3e 6*0 63 63 73 7b 7f 6f 67 63 63 63 6*0 f 6*6 66 66 3c 6*0 9*63 3e
  //   contents of rom_2 (hex, n*v repeats v):
  //   0 0 63 63 73 7b 7f 6f 67 63 63 63 6*0 f 6*6 66 66 3c 6*0 9*63 3e 6*0 1e 33 61 4*60 61 33 1e 6*0 3e
  //   63 63 30 1c 6 3 63 63 3e 6*0 63 63 73 7b 7f 6f 67 63 63 63 6*0 f 6*6 66 66 3c 6*0 9*63 3e
  //   contents of rom_3 (hex, n*v repeats v):
  //   0 0 63 63 73 7b 7f 6f 67 63 63 63 6*0 f 6*6 66 66 3c 6*0 9*63 3e 6*0 1e 33 61 4*60 61 33 1e 6*0 3e
  //   63 63 30 1c 6 3 63 63 3e 6*0 63 63 73 7b 7f 6f 67 63 63 63 6*0 f 6*6 66 66 3c 6*0 9*63 3e
  //   contents of rom_4 (hex, n*v repeats v):
  //   0 0 63 63 73 7b 7f 6f 67 63 63 63 6*0 f 6*6 66 66 3c 6*0 9*63 3e 6*0 1e 33 61 4*60 61 33 1e 6*0 3e
  //   63 63 30 1c 6 3 63 63 3e 6*0 63 63 73 7b 7f 6f 67 63 63 63 6*0 f 6*6 66 66 3c 6*0 9*63 3e
  //   contents of rom_5 (hex, n*v repeats v):
  //   0 0 63 63 73 7b 7f 6f 67 63 63 63 6*0 f 6*6 66 66 3c 6*0 9*63 3e 6*0 1e 33 61 4*60 61 33 1e 6*0 3e
  //   63 63 30 1c 6 3 63 63 3e 6*0 63 63 73 7b 7f 6f 67 63 63 63 6*0 f 6*6 66 66 3c 6*0 9*63 3e
  //   contents of rom_6 (hex, n*v repeats v):
  //   0 0 63 63 73 7b 7f 6f 67 63 63 63 6*0 f 6*6 66 66 3c 6*0 9*63 3e 6*0 1e 33 61 4*60 61 33 1e 6*0 3e
  //   63 63 30 1c 6 3 63 63 3e 6*0 63 63 73 7b 7f 6f 67 63 63 63 6*0 f 6*6 66 66 3c 6*0 9*63 3e
  //   contents of rom_7 (hex, n*v repeats v):
  //   0 0 63 63 73 7b 7f 6f 67 63 63 63 6*0 f 6*6 66 66 3c 6*0 9*63 3e 6*0 1e 33 61 4*60 61 33 1e 6*0 3e
  //   63 63 30 1c 6 3 63 63 3e 6*0 63 63 73 7b 7f 6f 67 63 63 63 6*0 f 6*6 66 66 3c 6*0 9*63 3e
  //   contents of rom_8 (hex, n*v repeats v):
  //   0 0 63 63 73 7b 7f 6f 67 63 63 63 6*0 f 6*6 66 66 3c 6*0 9*63 3e 6*0 1e 33 61 4*60 61 33 1e 6*0 3e
  //   63 63 30 1c 6 3 63 63 3e 6*0 63 63 73 7b 7f 6f 67 63 63 63 6*0 f 6*6 66 66 3c 6*0 9*63 3e
  //   contents of rom_9 (hex, n*v repeats v):
  //   0 0 63 63 73 7b 7f 6f 67 63 63 63 6*0 f 6*6 66 66 3c 6*0 9*63 3e 6*0 1e 33 61 4*60 61 33 1e 6*0 3e
  //   63 63 30 1c 6 3 63 63 3e 6*0 63 63 73 7b 7f 6f 67 63 63 63 6*0 f 6*6 66 66 3c 6*0 9*63 3e
  //   contents of rom_10 (hex, n*v repeats v):
  //   0 0 63 63 73 7b 7f 6f 67 63 63 63 6*0 f 6*6 66 66 3c 6*0 9*63 3e 6*0 1e 33 61 4*60 61 33 1e 6*0 3e
  //   63 63 30 1c 6 3 63 63 3e 6*0 63 63 73 7b 7f 6f 67 63 63 63 6*0 f 6*6 66 66 3c 6*0 9*63 3e
  //   contents of rom_11 (hex, n*v repeats v):
  //   0 0 63 63 73 7b 7f 6f 67 63 63 63 6*0 f 6*6 66 66 3c 6*0 9*63 3e 6*0 1e 33 61 4*60 61 33 1e 6*0 3e
  //   63 63 30 1c 6 3 63 63 3e 6*0 63 63 73 7b 7f 6f 67 63 63 63 6*0 f 6*6 66 66 3c 6*0 9*63 3e
  //   contents of rom_12 (hex, n*v repeats v):
  //   0 0 63 63 73 7b 7f 6f 67 63 63 63 6*0 f 6*6 66 66 3c 6*0 9*63 3e 6*0 1e 33 61 4*60 61 33 1e 6*0 3e
  //   63 63 30 1c 6 3 63 63 3e 6*0 63 63 73 7b 7f 6f 67 63 63 63 6*0 f 6*6 66 66 3c 6*0 9*63 3e
  //   contents of rom_13 (hex, n*v repeats v):
  //   0 0 63 63 73 7b 7f 6f 67 63 63 63 6*0 f 6*6 66 66 3c 6*0 9*63 3e 6*0 1e 33 61 4*60 61 33 1e 6*0 3e
  //   63 63 30 1c 6 3 63 63 3e 6*0 63 63 73 7b 7f 6f 67 63 63 63 6*0 f 6*6 66 66 3c 6*0 9*63 3e
  //   contents of rom_14 (hex, n*v repeats v):
  //   0 0 63 63 73 7b 7f 6f 67 63 63 63 6*0 f 6*6 66 66 3c 6*0 9*63 3e 6*0 1e 33 61 4*60 61 33 1e 6*0 3e
  //   63 63 30 1c 6 3 63 63 3e 6*0 63 63 73 7b 7f 6f 67 63 63 63 6*0 f 6*6 66 66 3c 6*0 9*63 3e
  //   contents of rom_15 (hex, n*v repeats v):
  //   0 0 63 63 73 7b 7f 6f 67 63 63 63 6*0 f 6*6 66 66 3c 6*0 9*63 3e 6*0 1e 33 61 4*60 61 33 1e 6*0 3e
  //   63 63 30 1c 6 3 63 63 3e 6*0 63 63 73 7b 7f 6f 67 63 63 63 6*0 f 6*6 66 66 3c 6*0 9*63 3e
  //   contents of rom_16 (hex, n*v repeats v):
  //   0 0 63 63 73 7b 7f 6f 67 63 63 63 6*0 f 6*6 66 66 3c 6*0 9*63 3e 6*0 1e 33 61 4*60 61 33 1e 6*0 3e
  //   63 63 30 1c 6 3 63 63 3e 6*0 63 63 73 7b 7f 6f 67 63 63 63 6*0 f 6*6 66 66 3c 6*0 9*63 3e
endmodule
