// Logisim project lab6.1.circ as structural Verilog: 3 circuits, main circuit 控制器
module \控制器  (
  input  [6:0] opcode,
  input  [2:0] funct3,
  input  [6:0] funct7,
  output [2:0] ExtOp,
  output RegWr,
  output [2:0] Branch,
  output ALUASrc,
  output [1:0] ALUBSrc,
  output [3:0] ALUctr,
  output MemtoReg,
  output [2:0] MemOp,
  output MemWr
);

  wire and_1_out, and_2_out, and_3_out, and_4_out, and_5_out, and_6_out, and_7_out, and_8_out, and_9_out,
       and_10_out, and_11_out, and_12_out, halt, I_Arith, J_jal, J_jalr, or_1_out, or_5_out, or_8_out,
       or_9_out, or_10_out, R_Arith, U_auipc, U_lui;

  Comparator #(.width(7)) comparator_1 (.a(opcode), .b(7'b0110111), .eq(U_lui));  // open: gt, lt
  Comparator #(.width(7)) comparator_2 (.a(opcode), .b(7'b1100111), .eq(J_jalr));  // open: gt, lt
  Comparator #(.width(7)) comparator_3 (.a(opcode), .b(7'b0010111), .eq(U_auipc));  // open: gt, lt
  Comparator #(.width(7)) comparator_4 (.a(opcode), .b(7'b1100011), .eq(Branch[2]));  // open: gt, lt
  or or_1 (or_1_out, U_lui, U_auipc);
  or or_2 (ALUBSrc[0], J_jal, J_jalr);
  and and_1 (and_1_out, Branch[2], funct3[2]);
  and and_2 (and_2_out, Branch[2], funct3[0]);
  and and_3 (and_3_out, funct3[2], ~funct3[1], funct3[0]);  // AND_Gate
  and and_4 (and_4_out, funct3[2], I_Arith);
  and and_5 (and_5_out, R_Arith, funct3[2]);
  and and_6 (and_6_out, funct3[1], I_Arith);
  and and_7 (and_7_out, funct3[1], R_Arith);
  and and_8 (and_8_out, R_Arith, funct3[0]);
  and and_9 (and_9_out, I_Arith, funct3[0]);
  and and_10 (and_10_out, Branch[2], funct3[1]);
  or or_3 (ALUASrc, U_auipc, ALUBSrc[0]);
  or or_4 (ALUBSrc[1], or_1_out, I_Arith, MemtoReg, MemWr);
  or or_5 (or_5_out, MemtoReg, MemWr);
  or or_6 (Branch[1], and_1_out, J_jalr);
  or or_7 (Branch[0], J_jal, and_2_out);
  and and_11 (and_11_out, and_3_out, funct7[5], I_Arith);
  and and_12 (and_12_out, R_Arith, funct7[5]);
  or or_8 (or_8_out, and_4_out, and_5_out);
  or or_9 (or_9_out, and_6_out, and_7_out, Branch[2]);
  or or_10 (or_10_out, and_8_out, and_9_out, and_10_out);
  Comparator #(.width(7)) comparator_5 (.a(opcode), .b(7'b0010011), .eq(I_Arith));  // open: gt, lt
  Comparator #(.width(7)) comparator_6 (.a(opcode), .b(7'b0000011), .eq(MemtoReg));  // open: gt, lt
  or or_11 (RegWr, or_1_out, ALUBSrc[0], I_Arith, R_Arith, MemtoReg);
  MenOp menop_1 (
    ._2(funct3[2]), ._1(funct3[1]), ._0(funct3[0]), .s(or_5_out), ._2_2(MemOp[2]), ._1_2(MemOp[1]),
    ._0_2(MemOp[0]));
  or or_12 (ALUctr[3], and_11_out, U_lui, and_12_out);
  or or_13 (ALUctr[2], U_lui, or_8_out);
  or or_14 (ALUctr[1], U_lui, or_9_out);
  or or_15 (ALUctr[0], U_lui, or_10_out);
  Comparator #(.width(7)) comparator_7 (.a(opcode), .b(7'b0110011), .eq(R_Arith));  // open: gt, lt
  Comparator #(.width(7)) comparator_8 (.a(opcode), .b(7'b0100011), .eq(MemWr));  // open: gt, lt
  Comparator #(.width(7)) comparator_9 (.a(opcode), .b(7'b1101111), .eq(J_jal));  // open: gt, lt
  Comparator #(.width(7)) comparator_10 (.a(opcode), .b({7{1'b0}}), .eq(halt));  // open: gt, lt
  ExtOp extop_1 (
    .a(opcode[6]), .b(opcode[5]), .c(opcode[4]), .d(opcode[3]), .e(opcode[2]), .f(opcode[1]), .g(opcode[0]),
    .x(ExtOp[2]), .y(ExtOp[1]), .z(ExtOp[0]));

  // Other names for the same wires on the sheet: B_Instr = Branch[2]; I_load = MemtoReg; S_Instr = MemWr

  // Notes on the sheet:
  //   输入引脚
  //   请勿修改引脚名称、电路名称及电路封装外观
  //   提示：根据指令种类，把7位指令code用一位指令类型标志位来表示，再通过功能码来区分具体指令，生成控制信号。
  //   输出引脚
endmodule

module ExtOp (
  input  a,
  input  b,
  input  c,
  input  d,
  input  e,
  input  f,
  input  g,
  output x,
  output y,
  output z
);

  wire and_3_out, and_4_out, and_5_out, comparator_1_eq, comparator_2_eq, not_1_out, not_2_out, not_3_out,
       not_4_out, or_1_out, or_2_out;

  Comparator #(.width(7), .mode("unsigned")) comparator_1 (
    .a({7{1'b0}}), .b({a, b, c, d, e, f, g}), .eq(comparator_1_eq));  // open: gt, lt
  Comparator #(.width(7), .mode("unsigned")) comparator_2 (
    .a(7'b0110011), .b({a, b, c, d, e, f, g}), .eq(comparator_2_eq));  // open: gt, lt
  not not_1 (not_1_out, f);
  not not_2 (not_2_out, e);
  not not_3 (not_3_out, a);
  not not_4 (not_4_out, e);
  and and_1 (x, ~comparator_1_eq, or_1_out);  // AND_Gate
  or or_1 (or_1_out, not_1_out, d);
  and and_2 (y, ~comparator_1_eq, ~comparator_2_eq, and_3_out);  // AND_Gate
  and and_3 (and_3_out, b, not_2_out);
  and and_4 (and_4_out, not_3_out, e);
  or or_2 (or_2_out, and_4_out, and_5_out);
  and and_5 (and_5_out, a, not_4_out);
  and and_6 (z, ~comparator_1_eq, or_2_out);  // AND_Gate
endmodule

module MenOp (
  input  _2,
  input  _1,
  input  _0,
  input  s,
  output _2_2,
  output _1_2,
  output _0_2
);

  wire and_1_out, and_2_out, not_1_out, not_2_out, not_3_out, not_4_out;

  not not_1 (not_1_out, _2);
  not not_2 (not_2_out, _1);
  not not_3 (not_3_out, _1);
  not not_4 (not_4_out, _0);
  and and_1 (and_1_out, not_1_out, not_2_out);
  and and_2 (and_2_out, not_3_out, not_4_out);
  and and_3 (_2_2, and_1_out, s);
  and and_4 (_1_2, _0, s);
  and and_5 (_0_2, and_2_out, s);
endmodule
