// Logisim project lab6.4.circ as structural Verilog: 16 circuits, main circuit main
module main (
  input  ReSet,
  input  [31:0] Init_Addr,
  input  clk,
  output [31:0] PC,
  output [31:0] IR,
  output [31:0] BusW,
  output [31:0] Din,
  output [15:0] Cycles,
  output Halt
);

  wire alu_1_zero, ALUASrc, clk_out, clk_t, MemToReg, MemWr, not_2_out, NxtASrc, NxtBSrc, RegWr;
  wire [1:0] ALUBSrc;
  wire [2:0] Branch, ExtOp, funct3, MemOp;
  wire [3:0] ALUctr;
  wire [6:0] funct7, opcode;
  wire [31:0] alu_1_s, dataram_1_dataout, idu_1_busa, idu_1_busb, idu_1_dataa, idu_1_datab, idu_1_imm;

  // Probe on Init_Addr
  IFU ifu_1 (
    .CLK(clk_t), .Reset(ReSet), .NxtASrc(NxtASrc), .NxtBSrc(NxtBSrc), .Initial_Address(Init_Addr),
    .Imm(idu_1_imm), .BusA(idu_1_busa), .PC(PC), .halt(Halt));
  \控制器  \u_控制器_1  (
    .opcode(opcode), .ExtOp(ExtOp), .RegWr(RegWr), .Branch(Branch), .funct3(funct3), .ALUASrc(ALUASrc),
    .ALUBSrc(ALUBSrc), .ALUctr(ALUctr), .funct7(funct7), .MemtoReg(MemToReg), .MemOp(MemOp), .MemWr(MemWr),
    .Halt(Halt));
  Clock u_clk (.out(clk_out));
  not not_1 (clk_t, clk_out);
  ROM #(.addrWidth(16), .dataWidth(32), .Select("high")) \u_指令存储器  (.addr(PC[17:2]), .data(IR));
  // Probe on PC
  // Probe on IR
  // Probe on BusW
  IDU idu_1 (
    .OpCode(opcode), .ExtOp(ExtOp), .RegWr(RegWr), .Imm(idu_1_imm), .Funct3(funct3), .ALUASrc(ALUASrc),
    .ALUBSrc(ALUBSrc), .Funct7(funct7), .CLK(clk_t), .IR(IR), .BusW(BusW), .PC(PC), .DataA(idu_1_dataa),
    .DataB(idu_1_datab), .BusA(idu_1_busa), .BusB(idu_1_busb));
  Multiplexer #(.width(32), .enable("false")) multiplexer_1 (.in0(idu_1_busb), .out(Din), .sel(ReSet));  // open: in1
  // Probe on Din
  ALU alu_1 (.A(idu_1_dataa), .B(idu_1_datab), .ALUctr(ALUctr), .S(alu_1_s), .Zero(alu_1_zero));
  Branch branch_1 (.Branch(Branch), .NxtASrc(NxtASrc), .Zero(alu_1_zero), .NxtBSrc(NxtBSrc), .Result0(alu_1_s[0]));
  DataRAM dataram_1 (
    .Addr(alu_1_s[17:0]), .Din(idu_1_busb), .CLK(clk_t), .CLR(ReSet), .WE(MemWr), .MemOp(MemOp),
    .DataOut(dataram_1_dataout));  // open: AlignErr
  // Probe on Cycles
  Counter #(.width(16), .max('hffff), .behavior("old")) \u_计数器  (
    .count(not_2_out), .Q(Cycles), .clk(clk_t), .clr(ReSet));  // open: load, D, carry, preset
  not not_2 (not_2_out, Halt);
  Multiplexer #(.width(32), .enable("false")) multiplexer_2 (
    .in0(alu_1_s), .in1(dataram_1_dataout), .out(BusW), .sel(MemToReg));

  // Notes on the sheet:
  //   输入引脚
  //   contents of 指令存储器 (hex, n*v repeats v):
  //   413 9117 ffc10113 2ec000ef 259693 d50833 50313 82883 60513 8c5d863 261793 f307b3 7a783 fff50713
  //   271713 e30733 70613 ffc70713 2f8d463 fff50513 472783 fea5c6e3 d30833 f82023 58513 f62023 1182023
  //   8067 d30833 251613 f82023 c30633 4a5d063 468713 e30733 70813 158593 470713 ffc72783 fca584e3
  //   fef8d6e3 f62023 2a5d063 259693 f85ff06f 58513 1182023 8067 58513 fa1ff06f 259813 1030833 58513
  //   f95ff06f 1ec5da63 fa010113 4812c23 5512223 3712e23 4112e23 4912a23 5212823 5312623 5412423 5612023
  //   3812c23 3912a23 3a12823 3b12623 58b93 60a93 50413 a8613 b8593 40513 ee5ff0ef a12223 fff50c93
  //   159bd663 c8613 b8593 40513 ec9ff0ef a12423 fff50d13 13abd263 d0613 b8593 40513 eadff0ef a12623
  //   fff50d93 fbbde63 d8613 b8593 40513 e91ff0ef a12823 fff50993 d3bda63 98613 b8593 40513 e75ff0ef
  //   fff50913 50493 b2bd863 90613 b8593 40513 e59ff0ef fff50b13 50a13 96bd663 b0613 b8593 40513 e3dff0ef
  //   a12a23 fff50c13 78bd263 c0613 b8593 40513 e21ff0ef fff50813 50713 50bd063 80613 b8593 40513 e12e23
  //   1012c23 dfdff0ef 50893 b8593 fff50613 40513 188b93 eadff0ef 1812803 1c12703 fd0bc4e3 170b93 fb8bc2e3
  //   1412783 178b93 f76bcee3 1a0b93 f52bcce3 148b93 f33bcae3 1012783 178b93 f1bbc6e3 c12783 178b93
  //   efabc2e3 812783 178b93 eb9bcee3 412783 178b93 e95bcae3 5c12083 5812403 5412483 5012903 4c12983
  //   4812a03 4412a83 4012b03 3c12b83 3812c03 3412c83 3012d03 2c12d83 6010113 8067 8067 ff010113 31400513
  //   1300613 593 112623 df5ff0ef c12083 513 1010113 8067 ff010113 31000513 112623 fcdff0ef 36a02223 6f 0
  //   4e20 1d4c0 53724e00 5b8d80 13d620 5dc 9896800 186a0 0 2bf20 2af8 b532b80 15f90 3e8 46 32 61a80
  //   2dc6c0 1f40 aa deadbeef
  //   请勿修改引脚名称、电路名称及电路封装外观
  //   指令存储器和数据存储器数据位都是32位，指令存储器编址以字为单位，数据存储器编址以字节为单位。
  //   引用取指令部件、取操作数部件、ALU部件、数据存储器、分支控制器、指令存储器等部件，完成单周期CPU设计。
  //   输出引脚
  //   状态元件的触发条件都设置成上升沿触发，时钟输入信号通过反相器输入。
  //   程序执行周期数
endmodule

module Branch (
  input  [2:0] Branch,
  input  Zero,
  input  Result0,
  output NxtASrc,
  output NxtBSrc
);

  wire not_1_out, or_1_out;

  not not_1 (not_1_out, Zero);
  or or_1 (or_1_out, ~Result0, Zero);  // OR_Gate
  Multiplexer #(.select(3), .enable("false")) multiplexer_1 (
    .in0(1'b0), .in1(1'b1), .in2(1'b1), .in4(Zero), .in5(not_1_out), .in6(Result0), .in7(or_1_out),
    .out(NxtBSrc), .sel(Branch));  // open: in3
  Multiplexer #(.select(3), .enable("false")) multiplexer_2 (
    .in0(1'b0), .in1(1'b0), .in2(1'b1), .in4(1'b0), .in5(1'b0), .in6(1'b0), .in7(1'b0), .out(NxtASrc),
    .sel(Branch));  // open: in3

  // Notes on the sheet:
  //   Zero: pull=down
  //   Branch: pull=down
  //   输入信号
  //   请勿修改引脚名称、电路名称及电路封装外观
  //   不要修改控制信号的编码定义、引脚名称和在布局中的位置。
  //   输出信号
endmodule

module IFU (
  input  [31:0] Initial_Address,
  input  [31:0] Imm,
  input  [31:0] BusA,
  input  CLK,
  input  Reset,
  input  halt,
  input  NxtASrc,
  input  NxtBSrc,
  output [31:0] PC
);

  wire not_1_out;
  wire [31:0] adder_1_out, multiplexer_1_out, multiplexer_2_out, multiplexer_3_out;

  Multiplexer #(.width(32), .enable("false")) multiplexer_1 (
    .in0(PC), .in1(BusA), .out(multiplexer_1_out), .sel(NxtASrc));
  Multiplexer #(.width(32), .enable("false")) multiplexer_2 (
    .in0(32'h4), .in1(Imm), .out(multiplexer_2_out), .sel(NxtBSrc));
  Adder #(.width(32)) adder_1 (.a(multiplexer_1_out), .b(multiplexer_2_out), .out(adder_1_out));  // open: cin, cout
  Multiplexer #(.width(32), .enable("false")) multiplexer_3 (
    .in0(adder_1_out), .in1(Initial_Address), .out(multiplexer_3_out), .sel(Reset));
  Register #(.width(32), .Select("high")) register_1 (
    .D(multiplexer_3_out), .en(not_1_out), .Q(PC), .clk(CLK));  // open: clr
  not not_1 (not_1_out, halt);

  // Other names for the same wires on the sheet: Init_Addr[31:0] = Initial_Address

  // Notes on the sheet:
  //   BusA: pull=down
  //   Imm: pull=down
  //   NxtBSrc: pull=down
  //   NxtASrc: pull=down
  //   输入信号
  //   请勿修改引脚名称、电路名称及电路封装外观
  //   指令存储器256KB，数据位为32位，地址位为16位。PC寄存器数据宽度32位，片选信号高电平有效
  //   输出信号
endmodule

module \控制器  (
  input  [6:0] opcode,
  input  [2:0] funct3,
  input  [6:0] funct7,
  output [2:0] ExtOp,
  output RegWr,
  output [2:0] Branch,
  output ALUASrc,
  output [1:0] ALUBSrc,
  output [3:0] ALUctr,
  output MemtoReg,
  output [2:0] MemOp,
  output MemWr,
  output Halt
);

  wire and_1_out, and_2_out, and_3_out, and_4_out, and_5_out, and_6_out, and_7_out, and_8_out, and_9_out,
       and_10_out, and_11_out, and_12_out, I_Arith, J_jal, J_jalr, or_1_out, or_5_out, or_8_out, or_9_out,
       or_10_out, R_Arith, U_auipc, U_lui;

  Comparator #(.width(7)) comparator_1 (.a(opcode), .b(7'b0110111), .eq(U_lui));  // open: gt, lt
  Comparator #(.width(7)) comparator_2 (.a(opcode), .b(7'b1100111), .eq(J_jalr));  // open: gt, lt
  Comparator #(.width(7)) comparator_3 (.a(opcode), .b(7'b0010111), .eq(U_auipc));  // open: gt, lt
  Comparator #(.width(7)) comparator_4 (.a(opcode), .b(7'b1100011), .eq(Branch[2]));  // open: gt, lt
  or or_1 (or_1_out, U_lui, U_auipc);
  or or_2 (ALUBSrc[0], J_jal, J_jalr);
  and and_1 (and_1_out, Branch[2], funct3[2]);
  and and_2 (and_2_out, Branch[2], funct3[0]);
  and and_3 (and_3_out, funct3[2], ~funct3[1], funct3[0]);  // AND_Gate
  and and_4 (and_4_out, funct3[2], I_Arith);
  and and_5 (and_5_out, R_Arith, funct3[2]);
  and and_6 (and_6_out, funct3[1], I_Arith);
  and and_7 (and_7_out, funct3[1], R_Arith);
  and and_8 (and_8_out, R_Arith, funct3[0]);
  and and_9 (and_9_out, I_Arith, funct3[0]);
  and and_10 (and_10_out, Branch[2], funct3[1]);
  or or_3 (ALUASrc, U_auipc, ALUBSrc[0]);
  or or_4 (ALUBSrc[1], or_1_out, I_Arith, MemtoReg, MemWr);
  or or_5 (or_5_out, MemtoReg, MemWr);
  or or_6 (Branch[1], and_1_out, J_jalr);
  or or_7 (Branch[0], J_jal, and_2_out);
  and and_11 (and_11_out, and_3_out, funct7[5], I_Arith);
  and and_12 (and_12_out, R_Arith, funct7[5]);
  or or_8 (or_8_out, and_4_out, and_5_out);
  or or_9 (or_9_out, and_6_out, and_7_out, Branch[2]);
  or or_10 (or_10_out, and_8_out, and_9_out, and_10_out);
  Comparator #(.width(7)) comparator_5 (.a(opcode), .b(7'b0010011), .eq(I_Arith));  // open: gt, lt
  Comparator #(.width(7)) comparator_6 (.a(opcode), .b(7'b0000011), .eq(MemtoReg));  // open: gt, lt
  or or_11 (RegWr, or_1_out, ALUBSrc[0], I_Arith, R_Arith, MemtoReg);
  MenOp menop_1 (
    ._2(funct3[2]), ._1(funct3[1]), ._0(funct3[0]), .s(or_5_out), ._2_2(MemOp[2]), ._1_2(MemOp[1]),
    ._0_2(MemOp[0]));
  or or_12 (ALUctr[3], and_11_out, U_lui, and_12_out);
  or or_13 (ALUctr[2], U_lui, or_8_out);
  or or_14 (ALUctr[1], U_lui, or_9_out);
  or or_15 (ALUctr[0], U_lui, or_10_out);
  Comparator #(.width(7)) comparator_7 (.a(opcode), .b(7'b0110011), .eq(R_Arith));  // open: gt, lt
  Comparator #(.width(7)) comparator_8 (.a(opcode), .b(7'b0100011), .eq(MemWr));  // open: gt, lt
  Comparator #(.width(7)) comparator_9 (.a(opcode), .b(7'b1101111), .eq(J_jal));  // open: gt, lt
  Comparator #(.width(7)) comparator_10 (.a(opcode), .b(7'b1110011), .eq(Halt));  // open: gt, lt
  ExtOp extop_1 (
    .a(opcode[6]), .b(opcode[5]), .c(opcode[4]), .d(opcode[3]), .e(opcode[2]), .f(opcode[1]), .g(opcode[0]),
    .x(ExtOp[2]), .y(ExtOp[1]), .z(ExtOp[0]));

  // Other names for the same wires on the sheet: B_Instr = Branch[2]; I_load = MemtoReg; S_Instr = MemWr

  // Notes on the sheet:
  //   输入引脚
  //   请勿修改引脚名称、电路名称及电路封装外观
  //   提示：根据指令种类，把7位指令code用一位指令类型标志位来表示，再通过功能码来区分具体指令，生成控制信号。
  //   输出引脚
endmodule

module IDU (
  input  [31:0] IR,
  input  [31:0] BusW,
  input  [31:0] PC,
  input  [2:0] ExtOp,
  input  RegWr,
  input  ALUASrc,
  input  [1:0] ALUBSrc,
  input  CLK,
  output [31:0] DataA,
  output [31:0] DataB,
  output [31:0] BusA,
  output [31:0] BusB,
  output [6:0] OpCode,
  output [31:0] Imm,
  output [2:0] Funct3,
  output [6:0] Funct7
);

  \立即数扩展器  \u_立即数扩展器_1  (.Instr(IR), .Extop(ExtOp), .imm(Imm));
  RegFile regfile_1 (
    .R1_num(IR[19:15]), .R2_num(IR[24:20]), .Write_Reg_num(IR[11:7]), .Write_Enable(RegWr), .Clock(CLK),
    .Din(BusW), .Reg1Out(BusA), .Reg2Out(BusB));
  Multiplexer #(.width(32), .enable("false")) multiplexer_1 (.in0(BusA), .in1(PC), .out(DataA), .sel(ALUASrc));
  Multiplexer #(.select(2), .width(32), .enable("false")) multiplexer_2 (
    .in0(BusB), .in1(32'h4), .in2(Imm), .out(DataB), .sel(ALUBSrc));  // open: in3

  assign Funct3 = IR[14:12];
  assign Funct7 = IR[31:25];
  assign OpCode = IR[6:0];

  // Other names for the same wires on the sheet: op[6:0] = IR[6:0]

  // Notes on the sheet:
  //   ALUBSrc: pull=down
  //   ExtOp: pull=down
  //   BusW: pull=down
  //   PC: pull=down
  //   RegWr: pull=down
  //   ALUASrc: pull=down
  //   输入信号
  //   为了后续实验中的引用，不要修改ALUASrc、ALUBSrc和EXtOP编码定义。
  //   请勿修改引脚名称、电路名称及电路封装外观
  //   输出信号
  //   修改寄存器堆电路设计，0号寄存器始终为0。
endmodule

module RegFile (
  input  [4:0] R1_num,
  input  [4:0] R2_num,
  input  [4:0] Write_Reg_num,
  input  [31:0] Din,
  input  Write_Enable,
  input  Clock,
  output [31:0] Reg1Out,
  output [31:0] Reg2Out
);

  wire and_1_out, and_2_out, and_3_out, and_4_out, and_5_out, and_6_out, and_7_out, and_8_out, and_9_out,
       and_10_out, and_11_out, and_12_out, and_13_out, and_14_out, and_15_out, and_16_out, and_17_out,
       and_18_out, and_19_out, and_20_out, and_21_out, and_22_out, and_23_out, and_24_out, and_25_out,
       and_26_out, and_27_out, and_28_out, and_29_out, and_30_out, and_31_out, and_32_out, decoder_1_out0,
       decoder_1_out1, decoder_1_out2, decoder_1_out3, decoder_1_out4, decoder_1_out5, decoder_1_out6,
       decoder_1_out7, decoder_1_out8, decoder_1_out9, decoder_1_out10, decoder_1_out11, decoder_1_out12,
       decoder_1_out13, decoder_1_out14, decoder_1_out15, decoder_1_out16, decoder_1_out17, decoder_1_out18,
       decoder_1_out19, decoder_1_out20, decoder_1_out21, decoder_1_out22, decoder_1_out23, decoder_1_out24,
       decoder_1_out25, decoder_1_out26, decoder_1_out27, decoder_1_out28, decoder_1_out29, decoder_1_out30,
       decoder_1_out31;
  wire [31:0] _0_q, _1_q, _2_q, _3_q, _4_q, _5_q, _6_q, _7_q, _8_q, _9_q, register_1_q, register_2_q,
       register_3_q, register_4_q, register_5_q, register_6_q, register_7_q, register_8_q, register_9_q,
       register_10_q, register_11_q, register_12_q, register_13_q, register_14_q, register_15_q,
       register_16_q, register_17_q, register_18_q, register_19_q, register_20_q, register_21_q,
       register_22_q;

  Decoder #(.select(5), .enable("false")) decoder_1 (
    .out0(decoder_1_out0), .out1(decoder_1_out1), .out2(decoder_1_out2), .out3(decoder_1_out3),
    .out4(decoder_1_out4), .out5(decoder_1_out5), .out6(decoder_1_out6), .out7(decoder_1_out7),
    .out8(decoder_1_out8), .out9(decoder_1_out9), .out10(decoder_1_out10), .out11(decoder_1_out11),
    .out12(decoder_1_out12), .out13(decoder_1_out13), .out14(decoder_1_out14), .out15(decoder_1_out15),
    .out16(decoder_1_out16), .out17(decoder_1_out17), .out18(decoder_1_out18), .out19(decoder_1_out19),
    .out20(decoder_1_out20), .out21(decoder_1_out21), .out22(decoder_1_out22), .out23(decoder_1_out23),
    .out24(decoder_1_out24), .out25(decoder_1_out25), .out26(decoder_1_out26), .out27(decoder_1_out27),
    .out28(decoder_1_out28), .out29(decoder_1_out29), .out30(decoder_1_out30), .out31(decoder_1_out31),
    .sel(Write_Reg_num));
  and and_1 (and_1_out, decoder_1_out0, Write_Enable);
  and and_2 (and_2_out, decoder_1_out1, Write_Enable);
  and and_3 (and_3_out, decoder_1_out2, Write_Enable);
  and and_4 (and_4_out, decoder_1_out3, Write_Enable);
  and and_5 (and_5_out, decoder_1_out4, Write_Enable);
  and and_6 (and_6_out, decoder_1_out5, Write_Enable);
  and and_7 (and_7_out, decoder_1_out6, Write_Enable);
  and and_8 (and_8_out, decoder_1_out7, Write_Enable);
  and and_9 (and_9_out, decoder_1_out8, Write_Enable);
  and and_10 (and_10_out, decoder_1_out9, Write_Enable);
  and and_11 (and_11_out, decoder_1_out10, Write_Enable);
  and and_12 (and_12_out, decoder_1_out11, Write_Enable);
  and and_13 (and_13_out, decoder_1_out12, Write_Enable);
  and and_14 (and_14_out, decoder_1_out13, Write_Enable);
  and and_15 (and_15_out, decoder_1_out14, Write_Enable);
  and and_16 (and_16_out, decoder_1_out15, Write_Enable);
  and and_17 (and_17_out, decoder_1_out16, Write_Enable);
  and and_18 (and_18_out, decoder_1_out17, Write_Enable);
  and and_19 (and_19_out, decoder_1_out18, Write_Enable);
  and and_20 (and_20_out, decoder_1_out19, Write_Enable);
  and and_21 (and_21_out, decoder_1_out20, Write_Enable);
  and and_22 (and_22_out, decoder_1_out21, Write_Enable);
  and and_23 (and_23_out, decoder_1_out22, Write_Enable);
  and and_24 (and_24_out, decoder_1_out23, Write_Enable);
  and and_25 (and_25_out, decoder_1_out24, Write_Enable);
  and and_26 (and_26_out, decoder_1_out25, Write_Enable);
  and and_27 (and_27_out, decoder_1_out26, Write_Enable);
  and and_28 (and_28_out, decoder_1_out27, Write_Enable);
  and and_29 (and_29_out, decoder_1_out28, Write_Enable);
  and and_30 (and_30_out, decoder_1_out29, Write_Enable);
  and and_31 (and_31_out, decoder_1_out30, Write_Enable);
  and and_32 (and_32_out, decoder_1_out31, Write_Enable);
  Register #(.width(32), .Select("high")) _0 (.en(and_1_out), .Q(_0_q), .clk(Clock));  // open: D, clr
  Register #(.width(32), .Select("high")) _1 (.D(Din), .en(and_2_out), .Q(_1_q), .clk(Clock));  // open: clr
  Register #(.width(32), .Select("high")) _2 (.D(Din), .en(and_3_out), .Q(_2_q), .clk(Clock));  // open: clr
  Register #(.width(32), .Select("high")) _3 (.D(Din), .en(and_4_out), .Q(_3_q), .clk(Clock));  // open: clr
  Register #(.width(32), .Select("high")) _4 (.D(Din), .en(and_5_out), .Q(_4_q), .clk(Clock));  // open: clr
  Register #(.width(32), .Select("high")) _5 (.D(Din), .en(and_6_out), .Q(_5_q), .clk(Clock));  // open: clr
  Register #(.width(32), .Select("high")) _6 (.D(Din), .en(and_7_out), .Q(_6_q), .clk(Clock));  // open: clr
  Register #(.width(32), .Select("high")) _7 (.D(Din), .en(and_8_out), .Q(_7_q), .clk(Clock));  // open: clr
  Register #(.width(32), .Select("high")) _8 (.D(Din), .en(and_9_out), .Q(_8_q), .clk(Clock));  // open: clr
  Register #(.width(32), .Select("high")) _9 (.D(Din), .en(and_10_out), .Q(_9_q), .clk(Clock));  // open: clr
  Register #(.width(32), .Select("high")) register_1 (
    .D(Din), .en(and_11_out), .Q(register_1_q), .clk(Clock));  // open: clr
  Register #(.width(32), .Select("high")) register_2 (
    .D(Din), .en(and_12_out), .Q(register_2_q), .clk(Clock));  // open: clr
  Register #(.width(32), .Select("high")) register_3 (
    .D(Din), .en(and_13_out), .Q(register_3_q), .clk(Clock));  // open: clr
  Register #(.width(32), .Select("high")) register_4 (
    .D(Din), .en(and_14_out), .Q(register_4_q), .clk(Clock));  // open: clr
  Register #(.width(32), .Select("high")) register_5 (
    .D(Din), .en(and_15_out), .Q(register_5_q), .clk(Clock));  // open: clr
  Register #(.width(32), .Select("high")) register_6 (
    .D(Din), .en(and_16_out), .Q(register_6_q), .clk(Clock));  // open: clr
  Register #(.width(32), .Select("high")) register_7 (
    .D(Din), .en(and_17_out), .Q(register_7_q), .clk(Clock));  // open: clr
  Register #(.width(32), .Select("high")) register_8 (
    .D(Din), .en(and_18_out), .Q(register_8_q), .clk(Clock));  // open: clr
  Register #(.width(32), .Select("high")) register_9 (
    .D(Din), .en(and_19_out), .Q(register_9_q), .clk(Clock));  // open: clr
  Register #(.width(32), .Select("high")) register_10 (
    .D(Din), .en(and_20_out), .Q(register_10_q), .clk(Clock));  // open: clr
  Register #(.width(32), .Select("high")) register_11 (
    .D(Din), .en(and_21_out), .Q(register_11_q), .clk(Clock));  // open: clr
  Register #(.width(32), .Select("high")) register_12 (
    .D(Din), .en(and_22_out), .Q(register_12_q), .clk(Clock));  // open: clr
  Register #(.width(32), .Select("high")) register_13 (
    .D(Din), .en(and_23_out), .Q(register_13_q), .clk(Clock));  // open: clr
  Register #(.width(32), .Select("high")) register_14 (
    .D(Din), .en(and_24_out), .Q(register_14_q), .clk(Clock));  // open: clr
  Register #(.width(32), .Select("high")) register_15 (
    .D(Din), .en(and_25_out), .Q(register_15_q), .clk(Clock));  // open: clr
  Register #(.width(32), .Select("high")) register_16 (
    .D(Din), .en(and_26_out), .Q(register_16_q), .clk(Clock));  // open: clr
  Register #(.width(32), .Select("high")) register_17 (
    .D(Din), .en(and_27_out), .Q(register_17_q), .clk(Clock));  // open: clr
  Register #(.width(32), .Select("high")) register_18 (
    .D(Din), .en(and_28_out), .Q(register_18_q), .clk(Clock));  // open: clr
  Register #(.width(32), .Select("high")) register_19 (
    .D(Din), .en(and_29_out), .Q(register_19_q), .clk(Clock));  // open: clr
  Register #(.width(32), .Select("high")) register_20 (
    .D(Din), .en(and_30_out), .Q(register_20_q), .clk(Clock));  // open: clr
  Register #(.width(32), .Select("high")) register_21 (
    .D(Din), .en(and_31_out), .Q(register_21_q), .clk(Clock));  // open: clr
  Register #(.width(32), .Select("high")) register_22 (
    .D(Din), .en(and_32_out), .Q(register_22_q), .clk(Clock));  // open: clr
  Multiplexer #(.select(5), .width(32), .enable("false")) multiplexer_1 (
    .in0(_0_q), .in1(_1_q), .in2(_2_q), .in3(_3_q), .in4(_4_q), .in5(_5_q), .in6(_6_q), .in7(_7_q),
    .in8(_8_q), .in9(_9_q), .in10(register_1_q), .in11(register_2_q), .in12(register_3_q),
    .in13(register_4_q), .in14(register_5_q), .in15(register_6_q), .in16(register_7_q), .in17(register_8_q),
    .in18(register_9_q), .in19(register_10_q), .in20(register_11_q), .in21(register_12_q),
    .in22(register_13_q), .in23(register_14_q), .in24(register_15_q), .in25(register_16_q),
    .in26(register_17_q), .in27(register_18_q), .in28(register_19_q), .in29(register_20_q),
    .in30(register_21_q), .in31(register_22_q), .out(Reg1Out), .sel(R1_num));
  Multiplexer #(.select(5), .width(32), .enable("false")) multiplexer_2 (
    .in0(_0_q), .in1(_1_q), .in2(_2_q), .in3(_3_q), .in4(_4_q), .in5(_5_q), .in6(_6_q), .in7(_7_q),
    .in8(_8_q), .in9(_9_q), .in10(register_1_q), .in11(register_2_q), .in12(register_3_q),
    .in13(register_4_q), .in14(register_5_q), .in15(register_6_q), .in16(register_7_q), .in17(register_8_q),
    .in18(register_9_q), .in19(register_10_q), .in20(register_11_q), .in21(register_12_q),
    .in22(register_13_q), .in23(register_14_q), .in24(register_15_q), .in25(register_16_q),
    .in26(register_17_q), .in27(register_18_q), .in28(register_19_q), .in29(register_20_q),
    .in30(register_21_q), .in31(register_22_q), .out(Reg2Out), .sel(R2_num));

  // Other names for the same wires on the sheet: CLK = Clock; RA[4:0] = R1_num; RB[4:0] = R2_num; RDA[31:0] = Reg1Out;
  //   RDB[31:0] = Reg2Out; RW[4:0] = Write_Reg_num; WE = Write_Enable

  // Notes on the sheet:
  //   输入引脚
  //   请勿修改引脚名称、电路名称及电路封装外观
  //   提示：使用译码器、多路选择器和32位寄存器及逻辑门实现寄存器堆，禁止直接使用存储器组件。
  //   输出引脚
endmodule

module \立即数扩展器  (
  input  [31:0] Instr,
  input  [2:0] Extop,
  output [31:0] imm
);

  wire [11:0] bit_extender_2_out;
  wire [19:0] bit_extender_1_out;
  wire [31:0] bit_extender_3_out, bit_extender_4_out;

  assign bit_extender_1_out = {{19{Instr[31]}}, Instr[31]};  // Bit_Extender bit_extender_1
  assign bit_extender_2_out = {{11{Instr[31]}}, Instr[31]};  // Bit_Extender bit_extender_2
  assign bit_extender_3_out = {{20{Instr[31]}}, Instr[31:20]};  // Bit_Extender bit_extender_3
  assign bit_extender_4_out = {{20{Instr[31]}}, {Instr[31:25], Instr[11:7]}};  // Bit_Extender bit_extender_4
  Multiplexer #(.select(3), .width(32), .enable("false")) multiplexer_1 (
    .in0(bit_extender_3_out), .in1({Instr[31:12], {12{1'b0}}}), .in2(bit_extender_4_out),
    .in3({bit_extender_1_out, Instr[7], Instr[30:25], Instr[11:8], 1'b0}),
    .in4({bit_extender_2_out, Instr[19:12], Instr[20], Instr[30:21], 1'b0}), .out(imm), .sel(Extop));  // open: in5, in6, in7

  // Notes on the sheet:
  //   Instr: pull=down
  //   Extop: pull=down
  //   输入引脚
  //   输出引脚
endmodule

module DataRAM (
  input  CLK,
  input  CLR,
  input  WE,
  input  [2:0] MemOp,
  input  [17:0] Addr,
  input  [31:0] Din,
  output AlignErr,
  output [31:0] DataOut
);

  wire and_1_out, and_2_out, and_3_out, and_4_out, and_5_out, and_6_out, and_7_out, and_8_out, and_9_out,
       and_10_out, and_11_out, and_12_out, and_13_out, and_14_out, and_15_out, and_16_out, and_17_out,
       and_18_out, and_19_out, and_20_out;
  wire [3:0] or_5_out;
  wire [7:0] multiplexer_1_out, multiplexer_2_out, multiplexer_3_out, multiplexer_4_out, multiplexer_5_out,
       ram_1_data, ram_2_data, ram_3_data, ram_4_data;
  wire [15:0] multiplexer_6_out;
  wire [31:0] bit_extender_1_out, bit_extender_2_out, bit_extender_3_out, bit_extender_4_out;

  Multiplexer #(.select(4), .width(8), .enable("false")) multiplexer_1 (
    .in8(Din[7:0]), .in12(Din[15:8]), .in15(Din[31:24]), .out(multiplexer_1_out), .sel(or_5_out));  // open: in0, in1, in2, in3, in4, in5, in6, in7, in9, in10, in11, in13, in14
  and and_1 (and_1_out, ~MemOp[0], ~MemOp[1], ~MemOp[2], ~Addr[0], ~Addr[1]);  // AND_Gate
  or or_1 (or_5_out[3], and_1_out, and_2_out, and_3_out);
  and and_2 (and_2_out, MemOp[0], ~MemOp[1], Addr[0], Addr[1]);  // AND_Gate
  and and_3 (and_3_out, ~MemOp[0], MemOp[1], ~Addr[0], Addr[1]);  // AND_Gate
  Multiplexer #(.select(4), .width(8), .enable("false")) multiplexer_2 (
    .in4(Din[7:0]), .in12(Din[7:0]), .in15(Din[23:16]), .out(multiplexer_2_out), .sel(or_5_out));  // open: in0, in1, in2, in3, in5, in6, in7, in8, in9, in10, in11, in13, in14
  and and_4 (and_4_out, Addr[0], ~Addr[1], ~MemOp[1], ~MemOp[0]);  // AND_Gate
  and and_5 (and_5_out, Addr[1], ~Addr[0], ~MemOp[0], ~MemOp[1]);  // AND_Gate
  and and_6 (and_6_out, Addr[1], Addr[0], ~MemOp[0], ~MemOp[1]);  // AND_Gate
  and and_7 (and_7_out, MemOp[2], ~MemOp[1], ~MemOp[0], ~Addr[0], ~Addr[1]);  // AND_Gate
  RAM #(.addrWidth(16), .bus("separate"), .Select("high"), .simpleMode("false")) ram_1 (
    .addr(Addr[17:2]), .din(multiplexer_1_out), .data(ram_1_data), .str(WE), .sel(or_5_out[3]), .clk(CLK),
    .clr(CLR));  // open: ld
  and and_8 (and_8_out, ~MemOp[0], ~MemOp[1], ~MemOp[2], ~Addr[0], ~Addr[1]);  // AND_Gate
  and and_9 (and_9_out, MemOp[0], ~MemOp[1], ~Addr[0], Addr[1]);  // AND_Gate
  and and_10 (and_10_out, ~MemOp[0], MemOp[1], ~Addr[0], Addr[1]);  // AND_Gate
  or or_2 (or_5_out[2], and_8_out, and_9_out, and_10_out);
  Multiplexer #(.select(4), .width(8), .enable("false")) multiplexer_3 (
    .in2(Din[7:0]), .in3(Din[15:8]), .in15(Din[15:8]), .out(multiplexer_3_out), .sel(or_5_out));  // open: in0, in1, in4, in5, in6, in7, in8, in9, in10, in11, in12, in13, in14
  RAM #(.addrWidth(16), .bus("separate"), .Select("high"), .simpleMode("false")) ram_2 (
    .addr(Addr[17:2]), .din(multiplexer_2_out), .data(ram_2_data), .str(WE), .sel(or_5_out[2]), .clk(CLK),
    .clr(CLR));  // open: ld
  and and_11 (and_11_out, ~MemOp[0], ~MemOp[1], ~MemOp[2], ~Addr[0], ~Addr[1]);  // AND_Gate
  and and_12 (and_12_out, MemOp[0], ~MemOp[1], Addr[0], ~Addr[1]);  // AND_Gate
  and and_13 (and_13_out, ~MemOp[0], MemOp[1], ~Addr[0], ~Addr[1]);  // AND_Gate
  and and_14 (and_14_out, Addr[0], ~Addr[1], MemOp[1], ~MemOp[0]);  // AND_Gate
  and and_15 (and_15_out, MemOp[1], ~MemOp[0], Addr[0], Addr[1]);  // AND_Gate
  and and_16 (and_16_out, MemOp[1], MemOp[0]);
  or or_3 (or_5_out[1], and_11_out, and_12_out, and_13_out);
  Multiplexer #(.select(4), .width(8), .enable("false")) multiplexer_4 (
    .in1(Din[7:0]), .in3(Din[7:0]), .in15(Din[7:0]), .out(multiplexer_4_out), .sel(or_5_out));  // open: in0, in2, in4, in5, in6, in7, in8, in9, in10, in11, in12, in13, in14
  RAM #(.addrWidth(16), .bus("separate"), .Select("high"), .simpleMode("false")) ram_3 (
    .addr(Addr[17:2]), .din(multiplexer_3_out), .data(ram_3_data), .str(WE), .sel(or_5_out[1]), .clk(CLK),
    .clr(CLR));  // open: ld
  and and_17 (and_17_out, ~MemOp[0], ~MemOp[1], ~MemOp[2], ~Addr[0], ~Addr[1]);  // AND_Gate
  and and_18 (and_18_out, MemOp[0], ~MemOp[1], ~Addr[0], ~Addr[1]);  // AND_Gate
  and and_19 (and_19_out, ~MemOp[0], MemOp[1], ~Addr[0], ~Addr[1]);  // AND_Gate
  or or_4 (AlignErr, and_4_out, and_5_out, and_6_out, and_7_out, and_14_out, and_15_out, and_16_out);
  RAM #(.addrWidth(16), .bus("separate"), .Select("high"), .simpleMode("false")) ram_4 (
    .addr(Addr[17:2]), .din(multiplexer_4_out), .data(ram_4_data), .str(WE), .sel(or_5_out[0]), .clk(CLK),
    .clr(CLR));  // open: ld
  or or_5 (or_5_out[0], and_17_out, and_18_out, and_19_out);
  Multiplexer #(.select(2), .width(8), .enable("false")) multiplexer_5 (
    .in0(ram_4_data), .in1(ram_3_data), .in2(ram_2_data), .in3(ram_1_data), .out(multiplexer_5_out),
    .sel(Addr[1:0]));
  assign bit_extender_1_out = {{24{multiplexer_5_out[7]}}, multiplexer_5_out};  // Bit_Extender bit_extender_1
  assign bit_extender_2_out = {{24{1'b0}}, multiplexer_5_out};  // Bit_Extender bit_extender_2
  assign bit_extender_3_out = {{16{1'b0}}, multiplexer_6_out};  // Bit_Extender bit_extender_3
  assign bit_extender_4_out = {{16{multiplexer_6_out[15]}}, multiplexer_6_out};  // Bit_Extender bit_extender_4
  Multiplexer #(.width(16), .enable("false")) multiplexer_6 (
    .in0({ram_3_data, ram_4_data}), .in1({ram_1_data, ram_2_data}), .out(multiplexer_6_out), .sel(and_20_out));
  and and_20 (and_20_out, ~Addr[0], Addr[1]);  // AND_Gate
  Multiplexer #(.select(3), .width(32), .enable("false")) multiplexer_7 (
    .in0({ram_1_data, ram_2_data, ram_3_data, ram_4_data}), .in1(bit_extender_2_out),
    .in2(bit_extender_3_out), .in5(bit_extender_1_out), .in6(bit_extender_4_out), .out(DataOut), .sel(MemOp));  // open: in3, in4, in7

  // Other names for the same wires on the sheet: Dout[31:0] = DataOut

  // Notes on the sheet:
  //   输入引脚
  //   输入引脚
  //   请勿修改引脚名称、电路名称及电路封装外观
  //   为了后续实验中的引用，不要修改MemOp的编码定义、引脚名称和在布局中的位置。
  //   32位数据存储器，按字节分4片存储，可按照字节、半字和字进行存储；读取字节或半字时，支持0扩展和符号位扩展。
  //   请勿修改引脚名称、电路名称及电路封装外观
  //   为了后续实验中的引用，不要修改MemOp的编码定义、引脚名称和在布局中的位置。
  //   32位数据存储器，按字节分4片存储，可按照字节、半字和字进行存储；读取字节或半字时，支持0扩展和符号位扩展。
  //   输出引脚
endmodule

module ALU (
  input  [3:0] ALUctr,
  input  [31:0] A,
  input  [31:0] B,
  output Zero,
  output [31:0] S
);

  wire adder32_1_cout, adder32_1_of, adder32_1_sf, aluctrl_1_alctr, aluctrl_1_sftctr, aluctrl_1_sigctr,
       aluctrl_1_subctr, multiplexer_2_out, xor_3_out, xor_4_out;
  wire [2:0] aluctrl_1_opctr;
  wire [31:0] adder32_1_s, and_1_out, bit_extender_1_out, bit_extender_2_out, or_1_out, shifter32_1_dataout,
       xor_1_out, xor_2_out;

  assign xor_1_out = B ^ bit_extender_1_out;  // XOR_Gate xor_1, 32 bits wide
  assign bit_extender_1_out = {{31{aluctrl_1_subctr}}, aluctrl_1_subctr};  // Bit_Extender bit_extender_1
  assign and_1_out = A & B;  // AND_Gate and_1, 32 bits wide
  assign or_1_out = A | B;  // OR_Gate or_1, 32 bits wide
  assign xor_2_out = A ^ B;  // XOR_Gate xor_2, 32 bits wide
  Shifter32 shifter32_1 (
    .DataIn(A), .shamt(B[4:0]), .L_R(aluctrl_1_sftctr), .A_L(aluctrl_1_alctr), .DataOut(shifter32_1_dataout));
  Adder32 adder32_1 (
    .OF(adder32_1_of), .SF(adder32_1_sf), .ZF(Zero), .X(A), .Y(xor_1_out), .Cin(aluctrl_1_subctr),
    .S(adder32_1_s), .Cout(adder32_1_cout));  // open: CF
  xor xor_3 (xor_3_out, aluctrl_1_subctr, adder32_1_cout);
  xor xor_4 (xor_4_out, adder32_1_of, adder32_1_sf);
  Multiplexer #(.select(3), .width(32), .enable("false")) multiplexer_1 (
    .in0(adder32_1_s), .in1(and_1_out), .in2(or_1_out), .in3(xor_2_out), .in4(shifter32_1_dataout), .in5(B),
    .in6(bit_extender_2_out), .in7({32{1'b0}}), .out(S), .sel(aluctrl_1_opctr));
  ALUctrl aluctrl_1 (
    .SUBctr(aluctrl_1_subctr), .SFTctr(aluctrl_1_sftctr), .SIGctr(aluctrl_1_sigctr), .ALctr(aluctrl_1_alctr),
    .OPctr(aluctrl_1_opctr), .ALUctr(ALUctr));
  // Probe on A
  // Probe on B
  // Probe on S
  Multiplexer #(.enable("false")) multiplexer_2 (
    .in0(xor_3_out), .in1(xor_4_out), .out(multiplexer_2_out), .sel(aluctrl_1_sigctr));
  assign bit_extender_2_out = {{31{1'b0}}, multiplexer_2_out};  // Bit_Extender bit_extender_2

  // Other names for the same wires on the sheet: Result[31:0] = S

  // Notes on the sheet:
  //   A: pull=down
  //   ALUctr: pull=down
  //   B: pull=down
  //   输入引脚
  //   请勿修改引脚名称、电路名称及电路封装外观
  //   提示：使用32位并行加法器子电路、桶形移位器、ALU控制子电路实现32位ALU
  //   功能说明:32位ALU，输入32位操作数A、B，4位控制信号ALUctr，输出32位结果Reseult和1位Zero标志位
  //   输出引脚
  //   操作数和结果
endmodule

module ALUctrl (
  input  [3:0] ALUctr,
  output SUBctr,
  output SFTctr,
  output SIGctr,
  output ALctr,
  output [2:0] OPctr
);

  wire and_1_out, and_2_out, and_3_out, and_4_out, and_5_out, and_6_out, and_7_out, and_8_out, and_9_out;

  and and_1 (and_1_out, ~ALUctr[3], ALUctr[2], ~ALUctr[1], ~ALUctr[0]);  // AND_Gate
  and and_2 (and_2_out, ALUctr[2], ALUctr[1], ALUctr[0]);
  and and_3 (and_3_out, ~ALUctr[3], ALUctr[2], ~ALUctr[0]);  // AND_Gate
  and and_4 (and_4_out, ~ALUctr[3], ~ALUctr[2], ALUctr[1]);  // AND_Gate
  and and_5 (and_5_out, ~ALUctr[3], ~ALUctr[1], ALUctr[0]);  // AND_Gate
  and and_6 (and_6_out, ~ALUctr[3], ~ALUctr[2], ALUctr[1]);  // AND_Gate
  and and_7 (and_7_out, ALUctr[3], ALUctr[2], ALUctr[0]);
  and and_8 (and_8_out, ~ALUctr[3], ~ALUctr[2], ALUctr[1]);  // AND_Gate
  or or_1 (SUBctr, and_8_out, and_9_out);
  and and_9 (and_9_out, ~ALUctr[0], ~ALUctr[1], ~ALUctr[2], ALUctr[3]);  // AND_Gate
  and and_10 (ALctr, ALUctr[0], ~ALUctr[1], ALUctr[2], ALUctr[3]);  // AND_Gate
  and and_11 (SFTctr, ALUctr[0], ~ALUctr[1], ~ALUctr[2], ~ALUctr[3]);  // AND_Gate
  or or_2 (OPctr[0], and_1_out, and_2_out);
  or or_3 (OPctr[1], and_3_out, and_4_out);
  or or_4 (OPctr[2], and_5_out, and_6_out, and_7_out);
  and and_12 (SIGctr, ~ALUctr[0], ALUctr[1], ~ALUctr[2], ~ALUctr[3]);  // AND_Gate

  // Other names for the same wires on the sheet: LRctr = SFTctr

  // Notes on the sheet:
  //   输入引脚
  //   ALU操作控制信号生成部件
  //   输出引脚
endmodule

module Adder32 (
  input  Cin,
  input  [31:0] X,
  input  [31:0] Y,
  output CF,
  output Cout,
  output OF,
  output SF,
  output [31:0] S,
  output ZF
);

  wire adder16_2_c16, and_1_out, and_2_out, or_2_out, or_3_out, or_4_out, or_5_out, or_6_out;

  Adder16 adder16_1 (.X(X[31:16]), .Y(Y[31:16]), .C0(adder16_2_c16), .S(S[31:16]), .C16(Cout));  // open: Pg, Gg
  xor xor_1 (CF, Cin, Cout);
  Adder16 adder16_2 (.X(X[15:0]), .Y(Y[15:0]), .C0(Cin), .S(S[15:0]), .C16(adder16_2_c16));  // open: Pg, Gg
  and and_1 (and_1_out, ~X[31], ~Y[31], S[31]);  // AND_Gate
  and and_2 (and_2_out, X[31], Y[31], ~S[31]);  // AND_Gate
  or or_1 (OF, and_1_out, and_2_out);
  // Probe on X
  // Probe on Y
  // Probe on S
  or or_2 (or_2_out, S[31], S[30], S[29], S[28], S[27], S[26], S[25], S[24]);
  or or_3 (or_3_out, S[23], S[22], S[21], S[20], S[19], S[18], S[17], S[16]);
  not not_1 (ZF, or_4_out);
  or or_4 (or_4_out, or_2_out, or_3_out, or_5_out, or_6_out);
  or or_5 (or_5_out, S[15], S[14], S[13], S[12], S[11], S[10], S[9], S[8]);
  or or_6 (or_6_out, S[7], S[6], S[5], S[4], S[3], S[2], S[1], S[0]);

  assign SF = S[31];

  // Notes on the sheet:
  //   Cin: pull=down
  //   Y: pull=down
  //   X: pull=down
  //   输入引脚区
  //   输出引脚区
  //   请勿修改引脚名称、电路名称及电路封装外观
  //   提示：使用16位并行加法器子电路实现32位快速加法器
  //   功能说明:32位Adder  S=X+Y，Cout为最高位进位位，Cin为进位输入， S为和，溢出OF、进位CF、零ZF、符号SF。
  //   +
  //   =
  //   无符号加法
endmodule

// 移位器
module Shifter32 (
  input  [4:0] shamt,
  input  L_R,
  input  A_L,
  input  [31:0] DataIn,
  output [31:0] DataOut
);

  wire and_1_out;
  wire [0:0] multiplexer_10_out;
  wire [1:0] bit_extender_4_out, multiplexer_8_out;
  wire [3:0] bit_extender_3_out, multiplexer_6_out;
  wire [7:0] bit_extender_2_out, multiplexer_4_out;
  wire [15:0] bit_extender_1_out, multiplexer_1_out;
  wire [31:0] multiplexer_3_out, multiplexer_5_out, multiplexer_7_out, multiplexer_9_out;
  wire [31:31] multiplexer_2_out;

  Multiplexer #(.width(16), .enable("false")) multiplexer_1 (
    .in0({16{1'b0}}), .in1(DataIn[31:16]), .out(multiplexer_1_out), .sel(and_1_out));
  and and_1 (and_1_out, L_R, A_L);
  Multiplexer #(.enable("false")) multiplexer_2 (.in0(1'b0), .in1(DataIn[31]), .out(multiplexer_2_out[31]), .sel(A_L));
  assign bit_extender_1_out = {{15{multiplexer_2_out[31]}}, multiplexer_2_out[31]};  // Bit_Extender bit_extender_1
  assign bit_extender_2_out = {{7{multiplexer_2_out[31]}}, multiplexer_2_out[31]};  // Bit_Extender bit_extender_2
  Multiplexer #(.select(2), .width(32), .enable("false")) multiplexer_3 (
    .in0(DataIn), .in1({bit_extender_1_out, DataIn[31:16]}), .in2(DataIn),
    .in3({DataIn[15:0], multiplexer_1_out}), .out(multiplexer_3_out), .sel({L_R, shamt[4]}));
  Multiplexer #(.width(8), .enable("false")) multiplexer_4 (
    .in0({8{1'b0}}), .in1(multiplexer_3_out[31:24]), .out(multiplexer_4_out), .sel(and_1_out));
  assign bit_extender_3_out = {{3{multiplexer_2_out[31]}}, multiplexer_2_out[31]};  // Bit_Extender bit_extender_3
  Multiplexer #(.select(2), .width(32), .enable("false")) multiplexer_5 (
    .in0(multiplexer_3_out), .in1({bit_extender_2_out, multiplexer_3_out[31:8]}), .in2(multiplexer_3_out),
    .in3({multiplexer_3_out[23:0], multiplexer_4_out}), .out(multiplexer_5_out), .sel({L_R, shamt[3]}));
  Multiplexer #(.width(4), .enable("false")) multiplexer_6 (
    .in0(4'b0000), .in1(multiplexer_5_out[31:28]), .out(multiplexer_6_out), .sel(and_1_out));
  assign bit_extender_4_out = {{1{multiplexer_2_out[31]}}, multiplexer_2_out[31]};  // Bit_Extender bit_extender_4
  Multiplexer #(.select(2), .width(32), .enable("false")) multiplexer_7 (
    .in0(multiplexer_5_out), .in1({bit_extender_3_out, multiplexer_5_out[31:4]}), .in2(multiplexer_5_out),
    .in3({multiplexer_5_out[27:0], multiplexer_6_out}), .out(multiplexer_7_out), .sel({L_R, shamt[2]}));
  Multiplexer #(.width(2), .enable("false")) multiplexer_8 (
    .in0(2'b00), .in1(multiplexer_7_out[31:30]), .out(multiplexer_8_out), .sel(and_1_out));
  Multiplexer #(.select(2), .width(32), .enable("false")) multiplexer_9 (
    .in0(multiplexer_7_out), .in1({bit_extender_4_out, multiplexer_7_out[31:2]}), .in2(multiplexer_7_out),
    .in3({multiplexer_7_out[29:0], multiplexer_8_out}), .out(multiplexer_9_out), .sel({L_R, shamt[1]}));
  Multiplexer #(.enable("false")) multiplexer_10 (
    .in0(1'b0), .in1(multiplexer_9_out[31]), .out(multiplexer_10_out[0]), .sel(and_1_out));
  Multiplexer #(.select(2), .width(32), .enable("false")) multiplexer_11 (
    .in0(multiplexer_9_out), .in1({multiplexer_2_out[31], multiplexer_9_out[31:1]}), .in2(multiplexer_9_out),
    .in3({multiplexer_9_out[30:0], multiplexer_10_out[0]}), .out(DataOut), .sel({L_R, shamt[0]}));

  // Other names for the same wires on the sheet: Din[31:0] = DataIn; Left_Right = L_R; Arth_Logic = A_L;
  //   Dout[31:0] = DataOut

  // Notes on the sheet:
  //   L/R,A/L: 00逻辑右移，01算术右移，10逻辑左移，11：循环左移
  //   输入引脚
  //   请勿修改引脚名称、电路名称及电路封装外观
  //   提示：使用多路选择器、逻辑门实现32位桶形移位器，禁止直接使用移位器组件。
  //   输出引脚
endmodule

module Adder16 (
  input  C0,
  input  [15:0] X,
  input  [15:0] Y,
  output C16,
  output Pg,
  output Gg,
  output [15:0] S
);

  wire cla4_1_gg, cla4_1_pg, cla4_2_gg, cla4_2_pg, cla4_3_gg, cla4_3_pg, cla4_4_gg, cla4_4_pg, clu4_1_c1,
       clu4_1_c2, clu4_1_c3;

  CLA4 cla4_1 (
    .X(X[15:12]), .F(S[15:12]), .Y(Y[15:12]), .Pg(cla4_1_pg), .Cin(clu4_1_c3), .Gg(cla4_1_gg));  // open: Cout
  CLA4 cla4_2 (.X(X[11:8]), .F(S[11:8]), .Y(Y[11:8]), .Pg(cla4_2_pg), .Cin(clu4_1_c2), .Gg(cla4_2_gg));  // open: Cout
  CLU4 clu4_1 (
    .P0(cla4_4_pg), .P1(cla4_3_pg), .P2(cla4_2_pg), .P3(cla4_1_pg), .C1(clu4_1_c1), .C3(clu4_1_c3),
    .G0(cla4_4_gg), .G1(cla4_3_gg), .G2(cla4_2_gg), .G3(cla4_1_gg), .C2(clu4_1_c2), .C4(C16), .C0(C0),
    .Pg(Pg), .Gg(Gg));
  CLA4 cla4_3 (.X(X[7:4]), .F(S[7:4]), .Y(Y[7:4]), .Pg(cla4_3_pg), .Cin(clu4_1_c1), .Gg(cla4_3_gg));  // open: Cout
  CLA4 cla4_4 (.X(X[3:0]), .F(S[3:0]), .Y(Y[3:0]), .Pg(cla4_4_pg), .Cin(C0), .Gg(cla4_4_gg));  // open: Cout
  // Probe on X
  // Probe on Y
  // Probe on S

  // Other names for the same wires on the sheet: S0[3:0] = S[3:0]; S1[3:0] = S[7:4]; S2[3:0] = S[11:8];
  //   S3[3:0] = S[15:12]

  // Notes on the sheet:
  //   X: pull=down
  //   C0: pull=down
  //   Y: pull=down
  //   输入引脚区
  //   请勿修改引脚名称、电路名称及电路封装外观
  //   提示：使用4位先行进位加法器和CLU子电路实现16位并行加法器
  //   功能说明:16位Adder  S=X+Y，C16为最高位进位位，C0为进位输入， Pg、Gg为成组进位生成传递函数
  //   输出引脚区
  //   +
  //   =
  //   无符号加法
endmodule

module CLA4 (
  input  [3:0] X,
  input  [3:0] Y,
  input  Cin,
  output [3:0] F,
  output Cout,
  output Pg,
  output Gg
);

  wire clu4_1_c1, clu4_1_c2, clu4_1_c3, fa_1_g, fa_1_p, fa_2_g, fa_2_p, fa_3_g, fa_3_p, fa_4_g, fa_4_p;

  Hex_Digit_Display hex_digit_display_1 (.value(X));  // open: dp
  FA fa_1 (.A(X[3]), .F(F[3]), .B(Y[3]), .P(fa_1_p), .Cin(clu4_1_c3), .G(fa_1_g));
  Hex_Digit_Display hex_digit_display_2 (.value(Y));  // open: dp
  FA fa_2 (.A(X[1]), .F(F[1]), .B(Y[1]), .P(fa_2_p), .Cin(clu4_1_c1), .G(fa_2_g));
  FA fa_3 (.A(X[2]), .F(F[2]), .B(Y[2]), .P(fa_3_p), .Cin(clu4_1_c2), .G(fa_3_g));
  Hex_Digit_Display hex_digit_display_3 (.value(F));  // open: dp
  CLU4 clu4_1 (
    .P0(fa_4_p), .P1(fa_2_p), .P2(fa_3_p), .P3(fa_1_p), .C1(clu4_1_c1), .C3(clu4_1_c3), .G0(fa_4_g),
    .G1(fa_2_g), .G2(fa_3_g), .G3(fa_1_g), .C2(clu4_1_c2), .C4(Cout), .C0(Cin), .Pg(Pg), .Gg(Gg));
  FA fa_4 (.A(X[0]), .F(F[0]), .B(Y[0]), .P(fa_4_p), .Cin(Cin), .G(fa_4_g));

  // Other names for the same wires on the sheet: Z[3:0] = F

  // Notes on the sheet:
  //   +
  //   =
  //   输出
  //   输入
  //   请勿修改引脚名称、电路名称及电路封装外观
  //   提示：使用全加器和CLU子电路实现四位先行进位加法器CLA4
endmodule

module CLU4 (
  input  P0,
  input  P1,
  input  P2,
  input  P3,
  input  G0,
  input  G1,
  input  G2,
  input  G3,
  input  C0,
  output C1,
  output C3,
  output C2,
  output C4,
  output Pg,
  output Gg
);

  wire and_1_out, and_2_out, and_3_out, and_4_out, and_5_out, and_6_out, and_8_out, and_9_out, and_10_out,
       and_11_out;

  and and_1 (and_1_out, C0, P0);
  or or_1 (C1, and_1_out, G0);
  and and_2 (and_2_out, G0, P1);
  and and_3 (and_3_out, C0, P0, P1);
  or or_2 (C2, and_2_out, and_3_out, G1);
  or or_3 (C3, and_6_out, and_5_out, and_4_out, G2);
  and and_4 (and_4_out, P2, P0, P1, C0);
  and and_5 (and_5_out, G0, P2, P1);
  and and_6 (and_6_out, G1, P2);
  or or_4 (C4, Gg, and_11_out);
  and and_7 (Pg, P0, P1, P2, P3);
  or or_5 (Gg, and_9_out, and_8_out, and_10_out, G3);
  and and_8 (and_8_out, P3, P2, G1);
  and and_9 (and_9_out, P3, G2);
  and and_10 (and_10_out, P1, P2, P3, G0);
  and and_11 (and_11_out, P0, P1, P2, P3, C0);

  // Notes on the sheet:
  //   输入引脚
  //   请勿修改引脚名称、电路名称及电路封装外观
  //   提示：使用逻辑门电路实现4位四位先行进位部件CLU，Pg、Gg为成组进位生成传递函数
  //   输出引脚
endmodule

module FA (
  input  A,
  input  B,
  input  Cin,
  output F,
  output P,
  output G
);

  wire xor_1_out;

  xor xor_1 (xor_1_out, A, Cin);
  or or_1 (P, B, A);
  and and_1 (G, B, A);
  xor xor_2 (F, xor_1_out, B);

  // Notes on the sheet:
  //   输入引脚
  //   请勿修改引脚名称、电路名称及电路封装外观
  //   输出引脚
endmodule
