// Logisim project lab6思考题.circ as structural Verilog: 1 circuit, main circuit main
module main (
  output RegWrite,
  output MemWrite,
  output [31:0] IF_PC,
  output [31:0] ID_PC,
  output [31:0] EX_PC,
  output [31:0] M_PC,
  output [31:0] WB_PC,
  output [31:0] RDin,
  output [31:0] MDin,
  output [31:0] LedData
);

  wire alu_2_p1, alu_2_p4, alu_2_p6, alu_2_p7, alu_2_p10, alu_2_p11, and_1_out, and_2_out, and_4_out, CLK,
       comparator_1_eq, comparator_2_eq, ecall, halt, not_1_out, not_2_out, or_1_out, regifile_1_p7,
       regifile_1_p8, RST, SType, \单周期硬布线控制器_1_p1 , \单周期硬布线控制器_1_p2 , \单周期硬布线控制器_1_p5 , \单周期硬布线控制器_1_p6 ,
       \单周期硬布线控制器_1_p7 , \单周期硬布线控制器_1_p8 , \单周期硬布线控制器_1_p9 , \单周期硬布线控制器_1_p10 , \单周期硬布线控制器_1_p11 ,
       \单周期硬布线控制器_1_p12 , \单周期硬布线控制器_1_p14 , \单周期硬布线控制器_1_p15 , \单周期硬布线控制器_1_p16 , \流水线通用组件_2_p13 ,
       \流水线通用组件_2_p14 , \流水线通用组件_2_p15 , \流水线通用组件_2_p16 , \流水线通用组件_2_p17 , \流水线通用组件_2_p18 , \流水线通用组件_2_p19 ,
       \流水线通用组件_2_p20 , \流水线通用组件_2_p21 , \流水线通用组件_2_p22 , \流水线通用组件_2_p23 , \流水线通用组件_2_p24 , \流水线通用组件_2_p25 ,
       \流水线通用组件_3_p14 , \流水线通用组件_3_p16 , \流水线通用组件_3_p17 , \流水线通用组件_3_p18 , \流水线通用组件_3_p19 , \流水线通用组件_3_p20 ,
       \流水线通用组件_3_p22 , \流水线通用组件_3_p23 , \流水线通用组件_3_p24 , \流水线通用组件_3_p25 , \流水线通用组件_3_p26 , \流水线通用组件_3_p27 ,
       \流水线通用组件_3_p28 , \流水线通用组件_3_p29 , \流水线通用组件_3_p30 , \流水线通用组件_4_p16 , \流水线通用组件_4_p17 , \流水线通用组件_4_p18 ,
       \流水线通用组件_4_p20 , \流水线通用组件_4_p21 ;
  wire [4:0] multiplexer_2_out, multiplexer_3_out;
  wire [7:0] multiplexer_5_out;
  wire [11:0] multiplexer_1_out;
  wire [11:2] undriven_2;
  wire [15:0] \LoadUse次数 , \总周期数 , \插入气泡数 , \无条件分支数 , \条件分支成功数 ;
  wire [31:0] adder_1_out, adder_2_out, adder_3_out, alu_2_p5, and_3_out, bit_extender_1_out,
       bit_extender_2_out, bit_extender_3_out, bit_extender_4_out, EX_IR, IF_IR, multiplexer_4_out,
       multiplexer_6_out, multiplexer_7_out, multiplexer_8_out, PC, ram_1_data, RegR1, RegR2, shifter_1_out,
       shifter_2_out, undriven, undriven_3, undriven_4, undriven_5, WB_IR;
  wire [31:2] ID_IR;

  Hex_Digit_Display hex_digit_display_1 (.value(LedData[31:28]));  // open: dp
  Hex_Digit_Display hex_digit_display_2 (.value(LedData[23:20]));  // open: dp
  Hex_Digit_Display hex_digit_display_3 (.value(LedData[27:24]));  // open: dp
  Hex_Digit_Display hex_digit_display_4 (.value(LedData[15:12]));  // open: dp
  Hex_Digit_Display hex_digit_display_5 (.value(LedData[19:16]));  // open: dp
  Register #(.width(32), .Select("low")) u_PC (.D(adder_1_out), .en(not_1_out), .Q(IF_PC), .clk(CLK), .clr(RST));
  not not_1 (not_1_out, halt);
  Hex_Digit_Display hex_digit_display_6 (.value(LedData[7:4]));  // open: dp
  Hex_Digit_Display hex_digit_display_7 (.value(LedData[11:8]));  // open: dp
  Clock clock_1 (.out(CLK));
  Hex_Digit_Display hex_digit_display_8 (.value(LedData[3:0]));  // open: dp
  // Probe on \总周期数 
  ROM #(.addrWidth(10), .dataWidth(32), .Select("high")) rom_1 (.addr(IF_PC[11:2]), .data(IF_IR));
  Adder #(.width(32)) adder_1 (.a(IF_PC), .b(32'h4), .out(adder_1_out));  // open: cin, cout
  // Probe on \总周期数 
  // Probe on \无条件分支数 
  // Probe on \条件分支成功数 
  // Probe on \插入气泡数 
  // Probe on \LoadUse次数 
  // Probe on IF_PC[11:0]
  // 流水线通用组件 流水线通用组件_1: pin names not known
  // Probe on EX_PC[11:0]
  // Probe on ID_PC[11:0]
  // Probe on M_PC[11:0]
  // Probe on WB_PC[11:0]
  // 单周期硬布线控制器 单周期硬布线控制器_1: pin names not known; wires that end beside it: \单周期硬布线控制器_1_p1 , \单周期硬布线控制器_1_p2 , ID_IR[6:2], {ID_IR[30], ID_IR[25], ID_IR[14:12]}, \单周期硬布线控制器_1_p5 , \单周期硬布线控制器_1_p6 , \单周期硬布线控制器_1_p7 , \单周期硬布线控制器_1_p8 , \单周期硬布线控制器_1_p9 , \单周期硬布线控制器_1_p10 , \单周期硬布线控制器_1_p11 , \单周期硬布线控制器_1_p12 , SType, \单周期硬布线控制器_1_p14 , \单周期硬布线控制器_1_p15 , \单周期硬布线控制器_1_p16 
  Multiplexer #(.width(12), .enable("false")) multiplexer_1 (
    .in0(ID_IR[31:20]), .in1({ID_IR[31:25], ID_IR[11:7]}), .out(multiplexer_1_out), .sel(SType));
  assign bit_extender_1_out = {{20{multiplexer_1_out[11]}}, multiplexer_1_out};  // Bit_Extender bit_extender_1
  assign bit_extender_2_out = {{20{ID_IR[31]}}, {ID_IR[31], ID_IR[7], ID_IR[30:25], ID_IR[11:8]}};  // Bit_Extender bit_extender_2
  assign bit_extender_3_out = {{12{ID_IR[31]}}, {ID_IR[31], ID_IR[19:12], ID_IR[20], ID_IR[30:21]}};  // Bit_Extender bit_extender_3
  Multiplexer #(.width(5), .enable("false")) multiplexer_2 (
    .in0(ID_IR[24:20]), .in1(5'b10001), .out(multiplexer_2_out), .sel(\单周期硬布线控制器_1_p5 ));
  Shifter #(.width(32)) shifter_1 (.in(bit_extender_2_out), .\dist (5'b00001), .out(shifter_1_out));
  Shifter #(.width(32)) shifter_2 (.in(bit_extender_3_out), .\dist (5'b00001), .out(shifter_2_out));
  Multiplexer #(.width(5), .enable("false")) multiplexer_3 (
    .in0(ID_IR[19:15]), .in1(5'b01010), .out(multiplexer_3_out), .sel(\单周期硬布线控制器_1_p5 ));
  Adder #(.width(32)) adder_2 (.a(PC), .b(shifter_1_out), .out(adder_2_out));  // open: cin, cout
  Adder #(.width(32)) adder_3 (.a(PC), .b(shifter_2_out), .out(adder_3_out));  // open: cin, cout
  // Regifile regifile_1: pin names not known; wires that end beside it: multiplexer_3_out, multiplexer_2_out, WB_IR[11:7], RDin, RegWrite, CLK, regifile_1_p7, regifile_1_p8, \单周期硬布线控制器_1_p16 , \单周期硬布线控制器_1_p5 , regifile_1_p7, regifile_1_p8, bit_extender_1_out, adder_2_out
  // 流水线通用组件 流水线通用组件_2: pin names not known; wires that end beside it: \单周期硬布线控制器_1_p2 , \单周期硬布线控制器_1_p1 , \单周期硬布线控制器_1_p6 , \单周期硬布线控制器_1_p7 , \单周期硬布线控制器_1_p8 , \单周期硬布线控制器_1_p9 , \单周期硬布线控制器_1_p10 , \单周期硬布线控制器_1_p11 , \单周期硬布线控制器_1_p12 , SType, \单周期硬布线控制器_1_p14 , \单周期硬布线控制器_1_p15 , \流水线通用组件_2_p13 , \流水线通用组件_2_p14 , \流水线通用组件_2_p15 , \流水线通用组件_2_p16 , \流水线通用组件_2_p17 , \流水线通用组件_2_p18 , \流水线通用组件_2_p19 , \流水线通用组件_2_p20 , \流水线通用组件_2_p21 , \流水线通用组件_2_p22 , \流水线通用组件_2_p23 , \流水线通用组件_2_p24 , \流水线通用组件_2_p25 
  Multiplexer #(.width(32), .enable("false")) multiplexer_4 (
    .in0(undriven), .in1(alu_2_p5), .out(multiplexer_4_out), .sel(\流水线通用组件_2_p20 ));
  // ALU alu_1: pin names not known
  // ALU alu_2: pin names not known; wires that end beside it: alu_2_p1, multiplexer_4_out, \流水线通用组件_2_p19 , alu_2_p4, alu_2_p5, alu_2_p6, alu_2_p7, EX_PC, EX_IR, alu_2_p10, alu_2_p11, CLK
  // 流水线通用组件 流水线通用组件_3: pin names not known; wires that end beside it: \流水线通用组件_2_p13 , \流水线通用组件_2_p14 , \流水线通用组件_2_p15 , \流水线通用组件_2_p16 , \流水线通用组件_2_p17 , \流水线通用组件_2_p18 , \流水线通用组件_2_p19 , \流水线通用组件_2_p20 , \流水线通用组件_2_p21 , \流水线通用组件_2_p22 , \流水线通用组件_2_p23 , \流水线通用组件_2_p24 , \流水线通用组件_2_p25 , \流水线通用组件_3_p14 , alu_2_p1, \流水线通用组件_3_p16 , \流水线通用组件_3_p17 , \流水线通用组件_3_p18 , \流水线通用组件_3_p19 , \流水线通用组件_3_p20 , MemWrite, \流水线通用组件_3_p22 , \流水线通用组件_3_p23 , \流水线通用组件_3_p24 , \流水线通用组件_3_p25 , \流水线通用组件_3_p26 , \流水线通用组件_3_p27 , \流水线通用组件_3_p28 , \流水线通用组件_3_p29 , \流水线通用组件_3_p30 
  and and_1 (and_1_out, CLK, ~halt);  // AND_Gate
  Counter #(.width(16), .max('hffff), .ongoal("stay"), .behavior("old")) counter_1 (
    .Q(\总周期数 ), .clk(and_1_out));  // open: load, D, count, carry, clr, preset
  RAM #(.addrWidth(10), .dataWidth(32), .bus("separate"), .Select("high"), .simpleMode("false")) ram_1 (
    .addr(undriven_2), .din(MDin), .data(ram_1_data), .str(MemWrite), .clk(CLK));  // open: sel, ld, clr
  // 流水线通用组件 流水线通用组件_4: pin names not known; wires that end beside it: \流水线通用组件_3_p16 , \流水线通用组件_3_p17 , \流水线通用组件_3_p18 , \流水线通用组件_3_p19 , \流水线通用组件_3_p20 , MemWrite, \流水线通用组件_3_p22 , \流水线通用组件_3_p23 , \流水线通用组件_3_p24 , \流水线通用组件_3_p25 , \流水线通用组件_3_p26 , \流水线通用组件_3_p27 , \流水线通用组件_3_p28 , \流水线通用组件_3_p29 , \流水线通用组件_3_p30 , \流水线通用组件_4_p16 , \流水线通用组件_4_p17 , \流水线通用组件_4_p18 , RegWrite, \流水线通用组件_4_p20 , \流水线通用组件_4_p21 , ecall, RegR1
  Comparator #(.width(32)) comparator_1 (.a(RegR2), .b(32'h22), .eq(comparator_1_eq));  // open: gt, lt
  and and_2 (and_2_out, ecall, comparator_1_eq);
  or or_1 (or_1_out, \流水线通用组件_4_p16 , \流水线通用组件_4_p17 );
  Multiplexer #(.select(2), .width(8), .enable("false")) multiplexer_5 (
    .in0(undriven_4[7:0]), .in1(undriven_4[15:8]), .in2(undriven_4[23:16]), .in3(undriven_4[31:24]),
    .out(multiplexer_5_out), .sel(undriven_3[1:0]));
  assign and_3_out = 32'hfffff000 & WB_IR;  // AND_Gate and_3, 32 bits wide
  Register #(.width(32), .Select("low")) register_1 (.D(RegR1), .en(and_2_out), .Q(LedData), .clk(CLK));  // open: clr
  assign bit_extender_4_out = {{24{multiplexer_5_out[7]}}, multiplexer_5_out};  // Bit_Extender bit_extender_4
  Multiplexer #(.width(32), .enable("false")) multiplexer_6 (
    .in0(undriven_4), .in1(bit_extender_4_out), .out(multiplexer_6_out), .sel(\流水线通用组件_4_p21 ));
  Multiplexer #(.width(32), .enable("false")) multiplexer_7 (
    .in0(undriven_3), .in1(multiplexer_6_out), .out(multiplexer_7_out), .sel(\流水线通用组件_4_p18 ));
  Comparator #(.width(32)) comparator_2 (.a(RegR2), .b(32'ha), .eq(comparator_2_eq));  // open: gt, lt
  Multiplexer #(.width(32), .enable("false")) multiplexer_8 (
    .in0(multiplexer_7_out), .in1(and_3_out), .out(multiplexer_8_out), .sel(\流水线通用组件_4_p20 ));
  Multiplexer #(.width(32), .enable("false")) multiplexer_9 (
    .in0(multiplexer_8_out), .in1(undriven_5), .out(RDin), .sel(or_1_out));
  and and_4 (and_4_out, ecall, comparator_2_eq);
  not not_2 (not_2_out, halt);
  Register #(.width(1), .Select("low")) register_2 (.D(and_4_out), .en(not_2_out), .Q(halt), .clk(CLK));  // open: clr

  // Other names for the same wires on the sheet: MEM_PC[31:0] = M_PC; WriteBack_Rd[4:0] = WB_IR[11:7];
  //   WriteBack_We = RegWrite

  // Notes on the sheet:
  //   contents of rom_1 (hex, n*v repeats v):
  //   413 493 913 993 46413 14e493 296913 39e993 842023 942223 1242423 1342623 a00893 493 913 993 73
  //   RS1
  //   RS2
  //   imm12
  //   a7
  //   a0
endmodule
